// Digital circuit CPU_secret_ready.dig as structural Verilog
module CPU_secret_ready (
  input  [7:0] M,
  input  [7:0] N,
  input  [13:0] progIn,
  input  reset,
  input  progLoad,
  input  start,
  input  result,
  input  clk,
  output valid,
  output done,
  output [7:0] \output 
);

  wire Branch_Condition_Met, Branch_Condition_Selected, Clear_Done_On_Stop, Comparator_Equal,
       Comparator_Greater, Comparator_Lesser, Compare_GCD_A_Equal_B, Compare_GCD_A_Greater_B,
       Compare_GCD_A_Lesser_B, Conditional_Jump_Active, Counter_Reached_15_Flag, DJNZ_Loop_Jump_Active,
       Done_Pre_Reset, Fib_Counter_Is_Zero, Fib_Registers_Clock_Enable, Fib_Step_Clock_Enable,
       Fib_Write_Active, Fib_Write_Byte_Toggle, Fibonacci_Finished_Flag, Fibonacci_Not_Finished, Flag_Equal,
       Flag_Equal_Enable, Flag_Equal_Write_Enable_Exec, Flag_Greater, Flag_Greater_Enable,
       Flag_Greater_Write_Enable_Exec, Flag_Lesser, Flags_Update_Operation, GCD_Clock_Enable,
       GCD_Done_Update_A, Hold_Done_Signal, Is_Branch_Subgroup_00, Is_Control_Group_Opcode,
       Is_Prime_Lookup_Result, Keep_Done_On_Stop, Loop5_Finished_Flag, Master_Clear_All_Pulse,
       Next_Done_Value, Next_Flag_Equal, Next_Flag_Greater, Next_Flag_Lesser, Next_SSUM_Done_Value,
       Next_SSUM_Write_Toggle, Next_State_Is_Out_State7, Next_State_Is_Stop_State6, Next_Valid_Value,
       Opcode_Is_CALL, Opcode_Is_CMP, Opcode_Is_DJNZ, Opcode_Is_FIB, Opcode_Is_FIB_Or_SSUM, Opcode_Is_GCD,
       Opcode_Is_PRAM_Access, Opcode_Is_PRIME, Opcode_Is_RET, Opcode_Is_SSUM, Opcode_Is_STOP,
       PC_Clock_Enable, PC_Enable_Execute, PC_Enable_Fib, PC_Enable_GCD, PC_Enable_Stage1, PC_Enable_Stage2,
       PC_Hold_In_Execute, PC_Step_In_Execute, pRAM_Address_Use_Operand, Register_D_Minus_1_Is_Zero,
       Register_D_Minus_1_Not_Zero, Reset_PC_and_SP_Pointers, rRAM_Write_Enable_Exec, rRAM_Write_Enable_Fib,
       rRAM_Write_Enable_Loop5, rRAM_Write_Strobe, Set_Done_Signal, SP_Is_Zero_Flag, SSUM_Done_Sum_Reg,
       SSUM_Finished_Flag, SSUM_Not_Done_Sum, SSUM_Ptr_Is_FF_Flag, SSUM_Registers_Clock_Enable,
       SSUM_Step_Clock_Enable, SSUM_Toggle_Clock_Enable, SSUM_Write_Active, SSUM_Write_Byte_Toggle,
       Stack_Pointer_Enable_Exec, Stack_Pointer_Write_Enable, Start_Fibonacci_Calculation,
       Start_GCD_Calculation, Start_SSUM_Calculation, State_Is_Clear_All, State_Is_Execute_Inst,
       State_Is_Fetch_Inst, State_Is_Fibonacci_Loop, State_Is_GCD_Loop, State_Is_Idle_Wait,
       State_Is_Loop5_Raw, State_Is_Output_Streaming, State_Is_Program_Halt, State_Is_SSUM_Loop,
       Target_Flag_Equal, Use_Loop_Counter_Select, Write_Enable_A, Write_Enable_A_In_Exec, Write_Enable_B,
       Write_Enable_B_In_Exec, Write_Enable_C, Write_Enable_C_In_Exec, Write_Enable_D, Write_Enable_D_In_Exec;
  wire [1:0] Instruction_Bits_11_10;
  wire [2:0] Current_State, Next_State_Clear_Logic, Next_State_Exec_Logic, Next_State_Exec_Stage1,
       Next_State_Exec_Stage2, Next_State_Fib_Logic, Next_State_GCD_Logic, Next_State_Idle_Logic,
       Next_State_Input, Next_State_Out_Logic, Next_State_Pre_Reset, Next_State_Stop_Logic,
       Next_State_Stop_Stage1, Next_State_Stop_Stage2;
  wire [3:0] Loop_Counter_4bit, Loop_Counter_Plus_1, Loop_Counter_Pre_Reset, Loop_Counter_Step,
       Next_Loop_Counter_Value;
  wire [4:0] Fib_Counter_Minus_1, Fib_Down_Counter, Next_Fib_Counter_Value;
  wire [5:0] Instruction_Opcode;
  wire [7:0] Accumulator_A, Accumulator_B, Add_Result, ALU_Result_Bus, Bitwise_AND_Result,
       Bitwise_NOT_Result, Bitwise_OR_Result, Bitwise_XOR_Result, Div_Quotient, Div_Remainder,
       Exec_RAM_Data_In, Fib_F0_High_Byte, Fib_F0_Low_Byte, Fib_RAM_Data_In, GCD_A_Minus_B, GCD_B_Minus_A,
       GCD_Register_A, GCD_Register_B, General_Register_C, General_Register_D, Instruction_Operand,
       Mul_Result, Multiplexed_Value_A, Next_GCD_A_Loop_Value, Next_GCD_A_Value, Next_GCD_B_Loop_Value,
       Next_GCD_B_Value, Next_PC_Value, Next_Program_Load_Address, Next_SP_In_Execute, Next_SSUM_Ptr_Value,
       Next_Stack_Pointer_Value, Next_Value_A, Next_Value_A_In_Exec, Next_Value_B, Next_Value_B_In_Exec,
       Next_Value_C, Next_Value_C_In_Exec, Next_Value_D, Next_Value_D_In_Exec, PC_Next_After_Call,
       PC_Next_Branch_Mux, PC_Next_In_Execute, pRAM_Address, pRAM_Address_Running, pRAM_Data_Low_8bit,
       Program_Counter, Program_Counter_Plus_1, Program_Load_Address, Program_Load_Address_Plus_1,
       Register_D_Minus_1, rRAM_Address, rRAM_Address_Exec, rRAM_Address_Fib, rRAM_Address_Fib_Or_Exec,
       rRAM_Address_Pre_Reset, rRAM_Address_Running, rRAM_Address_SSUM, rRAM_Data_In,
       rRAM_Data_In_Fib_Or_Exec, rRAM_Data_In_Running, Shift_Left_Result, Shift_Right_Result,
       SSUM_Pointer_Reg, SSUM_Ptr_Plus_1, SSUM_RAM_Data_In, SSUM_Write_Address, Stack_Pointer,
       Stack_Pointer_Minus_1, Stack_Pointer_Plus_1, Sub_Result;
  wire [13:8] pRAM_Data_Out;
  wire [15:0] Decoder_ROM_Output_16bit, Fib_Sum_F0_Plus_F1, Fib_Term_F1, Next_Fib_F0_Value,
       Next_Fib_F1_Value, Next_SSUM_Acc_Value, Rotate_Left_16bit_Double, Rotate_Right_16bit_Double,
       SSUM_Acc_16bit, SSUM_Acc_Plus_RAM;

  or or_1 (Master_Clear_All_Pulse, reset, State_Is_Clear_All);
  or or_2 (Reset_PC_and_SP_Pointers, Master_Clear_All_Pulse, start);
  or or_3 (PC_Hold_In_Execute, Opcode_Is_STOP, Opcode_Is_GCD, Opcode_Is_FIB_Or_SSUM);
  Sub #(.Bits(8)) sub_1 (.a(General_Register_D), .b(8'h1), .c_i(1'b0), .s(Register_D_Minus_1));  // open: c_o
  and and_1 (PC_Enable_Execute, State_Is_Execute_Inst, PC_Step_In_Execute);
  and and_2 (PC_Enable_GCD, State_Is_GCD_Loop, Compare_GCD_A_Equal_B);
  and and_3 (PC_Enable_Fib, State_Is_Loop5_Raw, Loop5_Finished_Flag);
  Multiplexer #(.Bits(8)) multiplexer_1 (
    .sel(Opcode_Is_CALL), .in_0(PC_Next_Branch_Mux), .in_1(Instruction_Operand), .out(PC_Next_After_Call));
  RAMDualPort #(.AddrBits(8), .Bits(14)) pRAM (
    .A(pRAM_Address), .Din(progIn), .str(progLoad), .C(clk), .ld(1'b1),
    .D({pRAM_Data_Out, pRAM_Data_Low_8bit}));
  Comparator #(.Bits(2)) comparator_1 (
    .a(Instruction_Opcode[5:4]), .b(2'b11), .eq(Is_Control_Group_Opcode));  // open: gt, lt
  Comparator #(.Bits(2)) comparator_2 (
    .a(Instruction_Bits_11_10), .b(2'b00), .eq(Is_Branch_Subgroup_00));  // open: gt, lt
  Comparator #(.Bits(8)) comparator_3 (
    .a(Register_D_Minus_1), .b({8{1'b0}}), .eq(Register_D_Minus_1_Is_Zero));  // open: gt, lt
  Add #(.Bits(8)) add_1 (.a(Program_Counter), .b(8'h1), .c_i(1'b0), .s(Program_Counter_Plus_1));  // open: c_o
  Multiplexer #(.Bits(8)) multiplexer_2 (
    .sel(Opcode_Is_RET), .in_0(PC_Next_After_Call), .in_1(\output ), .out(PC_Next_In_Execute));
  not not_1 (PC_Step_In_Execute, PC_Hold_In_Execute);
  or or_4 (PC_Enable_Stage1, Reset_PC_and_SP_Pointers, PC_Enable_Execute);
  or or_5 (PC_Enable_Stage2, PC_Enable_GCD, PC_Enable_Fib);
  Seven_Seg_Hex seven_seg_hex_1 (.d(\output [7:4]), .dp(1'b0));
  ROM #(.AddrBits(6), .Bits(16)) Decoder_ROM (
    .A({Instruction_Opcode[5:4], Instruction_Bits_11_10, Instruction_Opcode[1:0]}), .sel(1'b1),
    .D(Decoder_ROM_Output_16bit));
  RAMDualPort #(.AddrBits(8), .Bits(8)) rRAM (
    .A(rRAM_Address), .Din(rRAM_Data_In), .str(rRAM_Write_Strobe), .C(clk), .ld(1'b1), .D(\output ));
  Seven_Seg_Hex seven_seg_hex_2 (.d(\output [3:0]), .dp(1'b0));
  Multiplexer #(.Selector_Bits(2), .Bits(1)) multiplexer_3 (
    .sel(Instruction_Opcode[1:0]), .in_0(1'b1), .in_1(Flag_Equal), .in_2(Flag_Greater), .in_3(Flag_Lesser),
    .out(Branch_Condition_Selected));
  not not_2 (Register_D_Minus_1_Not_Zero, Register_D_Minus_1_Is_Zero);
  Multiplexer #(.Bits(8)) multiplexer_4 (
    .sel(Branch_Condition_Met), .in_0(Program_Counter_Plus_1), .in_1(Instruction_Operand),
    .out(PC_Next_Branch_Mux));
  or or_6 (PC_Clock_Enable, PC_Enable_Stage1, PC_Enable_Stage2);
  and and_4 (Conditional_Jump_Active, Is_Control_Group_Opcode, Is_Branch_Subgroup_00, Branch_Condition_Selected);
  or or_7 (Branch_Condition_Met, Conditional_Jump_Active, DJNZ_Loop_Jump_Active);
  and and_5 (DJNZ_Loop_Jump_Active, Opcode_Is_DJNZ, Register_D_Minus_1_Not_Zero);
  Multiplexer #(.Bits(8)) multiplexer_5 (
    .sel(Reset_PC_and_SP_Pointers), .in_0(PC_Next_In_Execute), .in_1({8{1'b0}}), .out(Next_PC_Value));
  Register #(.Bits(3)) STATE (.D(Next_State_Input), .C(clk), .en(1'b1), .Q(Current_State));
  Add #(.Bits(8)) add_2 (.a(Program_Load_Address), .b(8'h1), .c_i(1'b0), .s(Program_Load_Address_Plus_1));  // open: c_o
  Multiplexer #(.Bits(8)) multiplexer_6 (
    .sel(progLoad), .in_0({8{1'b0}}), .in_1(Program_Load_Address_Plus_1), .out(Next_Program_Load_Address));
  Register #(.Bits(8)) PC (.D(Next_PC_Value), .C(clk), .en(PC_Clock_Enable), .Q(Program_Counter));
  Register #(.Bits(1)) done_reg (.D(Next_Done_Value), .C(clk), .en(1'b1), .Q(done));
  Register #(.Bits(4)) cnt4 (.D(Next_Loop_Counter_Value), .C(clk), .en(1'b1), .Q(Loop_Counter_4bit));
  Register #(.Bits(8)) load_cnt (.D(Next_Program_Load_Address), .C(clk), .en(1'b1), .Q(Program_Load_Address));
  Register #(.Bits(1)) valid_reg (.D(Next_Valid_Value), .C(clk), .en(1'b1), .Q(valid));
  Register #(.Bits(14)) IR (
    .D({pRAM_Data_Out, pRAM_Data_Low_8bit}), .C(clk), .en(State_Is_Fetch_Inst),
    .Q({Instruction_Opcode[5:4], Instruction_Bits_11_10, Instruction_Opcode[1:0], Instruction_Operand}));
  and and_6 (State_Is_Fibonacci_Loop, State_Is_Loop5_Raw, Opcode_Is_FIB);
  Comparator #(.Signed("true"), .Bits(8)) comparator_4 (
    .a(Accumulator_A), .b(Accumulator_B), .gt(Comparator_Greater), .eq(Comparator_Equal),
    .lt(Comparator_Lesser));
  ROM #(.AddrBits(8), .Bits(1)) Prime_ROM (.A(Accumulator_A), .sel(1'b1), .D(Is_Prime_Lookup_Result));
  Multiplexer #(.Bits(1)) multiplexer_7 (
    .sel(Master_Clear_All_Pulse), .in_0(Target_Flag_Equal), .in_1(1'b0), .out(Next_Flag_Equal));
  Multiplexer #(.Bits(1)) multiplexer_8 (
    .sel(Master_Clear_All_Pulse), .in_0(Comparator_Greater), .in_1(1'b0), .out(Next_Flag_Greater));
  Multiplexer #(.Bits(1)) multiplexer_9 (
    .sel(Master_Clear_All_Pulse), .in_0(Comparator_Lesser), .in_1(1'b0), .out(Next_Flag_Lesser));
  Register #(.Bits(1)) FLAG_EQ (.D(Next_Flag_Equal), .C(clk), .en(Flag_Equal_Enable), .Q(Flag_Equal));
  Comparator #(.Bits(3)) comparator_5 (.a(Current_State), .b(3'b000), .eq(State_Is_Clear_All));  // open: gt, lt
  Comparator #(.Bits(3)) comparator_6 (.a(Current_State), .b(3'b001), .eq(State_Is_Idle_Wait));  // open: gt, lt
  Comparator #(.Bits(3)) comparator_7 (.a(Current_State), .b(3'b010), .eq(State_Is_Fetch_Inst));  // open: gt, lt
  Comparator #(.Bits(3)) comparator_8 (.a(Current_State), .b(3'b011), .eq(State_Is_Execute_Inst));  // open: gt, lt
  Comparator #(.Bits(3)) comparator_9 (.a(Current_State), .b(3'b100), .eq(State_Is_GCD_Loop));  // open: gt, lt
  Comparator #(.Bits(3)) comparator_10 (.a(Current_State), .b(3'b101), .eq(State_Is_Loop5_Raw));  // open: gt, lt
  Comparator #(.Bits(3)) comparator_11 (.a(Current_State), .b(3'b110), .eq(State_Is_Program_Halt));  // open: gt, lt
  Comparator #(.Bits(3)) comparator_12 (.a(Current_State), .b(3'b111), .eq(State_Is_Output_Streaming));  // open: gt, lt
  Add #(.Bits(4)) add_3 (.a(Loop_Counter_4bit), .b(4'b0001), .c_i(1'b0), .s(Loop_Counter_Plus_1));  // open: c_o
  Comparator #(.Bits(4)) comparator_13 (
    .a(Loop_Counter_4bit), .b(4'b1111), .eq(Counter_Reached_15_Flag));  // open: gt, lt
  Register #(.Bits(1)) FLAG_GR (.D(Next_Flag_Greater), .C(clk), .en(Flag_Greater_Enable), .Q(Flag_Greater));
  and and_7 (State_Is_SSUM_Loop, State_Is_Loop5_Raw, Opcode_Is_SSUM);
  Multiplexer #(.Bits(1)) multiplexer_10 (
    .sel(Opcode_Is_PRIME), .in_0(Comparator_Equal), .in_1(Is_Prime_Lookup_Result), .out(Target_Flag_Equal));
  or or_8 (Flags_Update_Operation, Opcode_Is_CMP, Opcode_Is_PRIME);
  or or_9 (Flag_Equal_Enable, Master_Clear_All_Pulse, Flag_Equal_Write_Enable_Exec);
  and and_8 (Flag_Equal_Write_Enable_Exec, State_Is_Execute_Inst, Flags_Update_Operation);
  or or_10 (Flag_Greater_Enable, Master_Clear_All_Pulse, Flag_Greater_Write_Enable_Exec);
  and and_9 (Flag_Greater_Write_Enable_Exec, State_Is_Execute_Inst, Opcode_Is_CMP);
  Register #(.Bits(1)) FLAG_LS (.D(Next_Flag_Lesser), .C(clk), .en(Flag_Greater_Enable), .Q(Flag_Lesser));
  Multiplexer #(.Bits(3)) multiplexer_11 (
    .sel(Counter_Reached_15_Flag), .in_0(3'b000), .in_1(3'b001), .out(Next_State_Clear_Logic));
  Multiplexer #(.Bits(3)) multiplexer_12 (.sel(start), .in_0(3'b001), .in_1(3'b010), .out(Next_State_Idle_Logic));
  Multiplexer #(.Bits(3)) multiplexer_13 (
    .sel(start), .in_0(Next_State_Stop_Stage1), .in_1(3'b010), .out(Next_State_Stop_Stage2));
  Comparator #(.Bits(6)) comparator_14 (
    .a({Instruction_Opcode[5:4], Instruction_Bits_11_10, Instruction_Opcode[1:0]}), .b({6{1'b1}}),
    .eq(Opcode_Is_STOP));  // open: gt, lt
  Comparator #(.Bits(6)) comparator_15 (
    .a({Instruction_Opcode[5:4], Instruction_Bits_11_10, Instruction_Opcode[1:0]}), .b(6'b111100),
    .eq(Opcode_Is_GCD));  // open: gt, lt
  Comparator #(.Bits(6)) comparator_16 (
    .a({Instruction_Opcode[5:4], Instruction_Bits_11_10, Instruction_Opcode[1:0]}), .b(6'b111101),
    .eq(Opcode_Is_FIB));  // open: gt, lt
  Comparator #(.Bits(6)) comparator_17 (
    .a({Instruction_Opcode[5:4], Instruction_Bits_11_10, Instruction_Opcode[1:0]}), .b(6'b111000),
    .eq(Opcode_Is_CMP));  // open: gt, lt
  Comparator #(.Bits(6)) comparator_18 (
    .a({Instruction_Opcode[5:4], Instruction_Bits_11_10, Instruction_Opcode[1:0]}), .b(6'b111001),
    .eq(Opcode_Is_PRIME));  // open: gt, lt
  Comparator #(.Bits(6)) comparator_19 (
    .a({Instruction_Opcode[5:4], Instruction_Bits_11_10, Instruction_Opcode[1:0]}), .b(6'b110100),
    .eq(Opcode_Is_DJNZ));  // open: gt, lt
  Comparator #(.Bits(6)) comparator_20 (
    .a({Instruction_Opcode[5:4], Instruction_Bits_11_10, Instruction_Opcode[1:0]}), .b(6'b010010),
    .eq(Opcode_Is_PRAM_Access));  // open: gt, lt
  Add #(.Bits(8)) add_4 (.a(Accumulator_A), .b(Accumulator_B), .c_i(1'b0), .s(Add_Result));  // open: c_o
  Sub #(.Bits(8)) sub_2 (.a(Accumulator_A), .b(Accumulator_B), .c_i(1'b0), .s(Sub_Result));  // open: c_o
  Div #(.Bits(8)) div_1 (.a(Accumulator_A), .b(Accumulator_B), .q(Div_Quotient), .r(Div_Remainder));
  assign Bitwise_AND_Result = Accumulator_A & Accumulator_B;  // And and_10, 8 bits wide
  assign Bitwise_OR_Result = Accumulator_A | Accumulator_B;  // Or or_11, 8 bits wide
  assign Bitwise_XOR_Result = Accumulator_A ^ Accumulator_B;  // XOr xor_1, 8 bits wide
  assign Bitwise_NOT_Result = ~Accumulator_A;  // Not not_3, 8 bits wide
  BarrelShifter #(.Bits(8), .direction("left")) barrelshifter_1 (
    .in(Accumulator_A), .shift({1'b0, Accumulator_B[2:0]}), .out(Shift_Left_Result));
  BarrelShifter #(.Bits(16), .direction("left")) barrelshifter_2 (
    .in({Accumulator_A, Accumulator_A}), .shift({2'b00, Accumulator_B[2:0]}), .out(Rotate_Left_16bit_Double));
  Multiplexer #(.Bits(3)) multiplexer_14 (
    .sel(Counter_Reached_15_Flag), .in_0(3'b111), .in_1(3'b110), .out(Next_State_Out_Logic));
  Multiplexer #(.Bits(3)) multiplexer_15 (
    .sel(result), .in_0(Next_State_Stop_Stage2), .in_1(3'b111), .out(Next_State_Stop_Logic));
  Multiplexer #(.Bits(3)) multiplexer_16 (.sel(progLoad), .in_0(3'b110), .in_1(3'b001), .out(Next_State_Stop_Stage1));
  Multiplexer #(.Bits(3)) multiplexer_17 (
    .sel(Opcode_Is_STOP), .in_0(Next_State_Exec_Stage2), .in_1(3'b110), .out(Next_State_Exec_Logic));
  Multiplexer #(.Bits(3)) multiplexer_18 (
    .sel(Opcode_Is_GCD), .in_0(Next_State_Exec_Stage1), .in_1(3'b100), .out(Next_State_Exec_Stage2));
  Multiplexer #(.Bits(3)) multiplexer_19 (
    .sel(Opcode_Is_FIB_Or_SSUM), .in_0(3'b010), .in_1(3'b101), .out(Next_State_Exec_Stage1));
  Multiplexer #(.Bits(3)) multiplexer_20 (
    .sel(Compare_GCD_A_Equal_B), .in_0(3'b100), .in_1(3'b010), .out(Next_State_GCD_Logic));
  Multiplexer #(.Bits(3)) multiplexer_21 (
    .sel(Loop5_Finished_Flag), .in_0(3'b101), .in_1(3'b010), .out(Next_State_Fib_Logic));
  Comparator #(.Bits(6)) comparator_21 (
    .a({Instruction_Opcode[5:4], Instruction_Bits_11_10, Instruction_Opcode[1:0]}), .b(6'b011100),
    .eq(Opcode_Is_CALL));  // open: gt, lt
  Comparator #(.Bits(6)) comparator_22 (
    .a({Instruction_Opcode[5:4], Instruction_Bits_11_10, Instruction_Opcode[1:0]}), .b(6'b011101),
    .eq(Opcode_Is_RET));  // open: gt, lt
  Comparator #(.Bits(6)) comparator_23 (
    .a({Instruction_Opcode[5:4], Instruction_Bits_11_10, Instruction_Opcode[1:0]}), .b(6'b111110),
    .eq(Opcode_Is_SSUM));  // open: gt, lt
  BarrelShifter #(.Bits(8), .direction("right")) barrelshifter_3 (
    .in(Accumulator_A), .shift({1'b0, Accumulator_B[2:0]}), .out(Shift_Right_Result));
  BarrelShifter #(.Bits(16), .direction("right")) barrelshifter_4 (
    .in({Accumulator_A, Accumulator_A}), .shift({2'b00, Accumulator_B[2:0]}), .out(Rotate_Right_16bit_Double));
  Multiplexer #(.Selector_Bits(3), .Bits(3)) multiplexer_22 (
    .sel(Current_State), .in_0(Next_State_Clear_Logic), .in_1(Next_State_Idle_Logic), .in_2(3'b011),
    .in_3(Next_State_Exec_Logic), .in_4(Next_State_GCD_Logic), .in_5(Next_State_Fib_Logic),
    .in_6(Next_State_Stop_Logic), .in_7(Next_State_Out_Logic), .out(Next_State_Pre_Reset));
  Multiplexer #(.Bits(4)) multiplexer_23 (
    .sel(Counter_Reached_15_Flag), .in_0(Loop_Counter_Plus_1), .in_1(4'b0000), .out(Loop_Counter_Step));
  Multiplexer #(.Bits(4)) multiplexer_24 (
    .sel(Use_Loop_Counter_Select), .in_0(4'b0000), .in_1(Loop_Counter_Step), .out(Loop_Counter_Pre_Reset));
  or or_12 (Use_Loop_Counter_Select, State_Is_Clear_All, State_Is_Output_Streaming);
  and and_11 (Set_Done_Signal, State_Is_Output_Streaming, Counter_Reached_15_Flag);
  or or_13 (Clear_Done_On_Stop, result, start, progLoad);
  not not_4 (Keep_Done_On_Stop, Clear_Done_On_Stop);
  and and_12 (Hold_Done_Signal, State_Is_Program_Halt, done, Keep_Done_On_Stop);
  or or_14 (Opcode_Is_FIB_Or_SSUM, Opcode_Is_FIB, Opcode_Is_SSUM);
  Mul #(.Bits(4)) mul_1 (.a(Accumulator_A[3:0]), .b(Accumulator_B[3:0]), .mul(Mul_Result));
  Multiplexer #(.Bits(3)) multiplexer_25 (
    .sel(reset), .in_0(Next_State_Pre_Reset), .in_1(3'b000), .out(Next_State_Input));
  Multiplexer #(.Bits(4)) multiplexer_26 (
    .sel(reset), .in_0(Loop_Counter_Pre_Reset), .in_1(4'b0000), .out(Next_Loop_Counter_Value));
  Comparator #(.Bits(3)) comparator_24 (
    .a(Next_State_Input), .b(3'b110), .gt(Next_State_Is_Out_State7), .eq(Next_State_Is_Stop_State6));  // open: lt
  or or_15 (Next_Valid_Value, Next_State_Is_Out_State7, Next_State_Is_Stop_State6);
  or or_16 (Done_Pre_Reset, Set_Done_Signal, Hold_Done_Signal);
  Multiplexer #(.Bits(1)) multiplexer_27 (.sel(reset), .in_0(Done_Pre_Reset), .in_1(1'b0), .out(Next_Done_Value));
  Multiplexer #(.Selector_Bits(4), .Bits(8)) multiplexer_28 (
    .sel({Instruction_Bits_11_10, Instruction_Opcode[1:0]}), .in_0(Add_Result), .in_1(Sub_Result),
    .in_2(Mul_Result), .in_3({8{1'b0}}), .in_4(Div_Quotient), .in_5(Div_Remainder), .in_6({8{1'b0}}),
    .in_7({8{1'b0}}), .in_8(Bitwise_AND_Result), .in_9(Bitwise_OR_Result), .in_10(Bitwise_XOR_Result),
    .in_11(Bitwise_NOT_Result), .in_12(Shift_Left_Result), .in_13(Shift_Right_Result),
    .in_14(Rotate_Left_16bit_Double[15:8]), .in_15(Rotate_Right_16bit_Double[7:0]), .out(ALU_Result_Bus));
  Comparator #(.Bits(8)) comparator_25 (
    .a(GCD_Register_A), .b(GCD_Register_B), .gt(Compare_GCD_A_Greater_B), .eq(Compare_GCD_A_Equal_B),
    .lt(Compare_GCD_A_Lesser_B));
  Sub #(.Bits(8)) sub_3 (.a(Stack_Pointer), .b(8'h1), .c_i(1'b0), .s(Stack_Pointer_Minus_1));  // open: c_o
  Add #(.Bits(8)) add_5 (.a(Stack_Pointer), .b(8'h1), .c_i(1'b0), .s(Stack_Pointer_Plus_1));  // open: c_o
  Multiplexer #(.Bits(8)) multiplexer_29 (
    .sel(Decoder_ROM_Output_16bit[6]), .in_0(Instruction_Operand), .in_1(Accumulator_A),
    .out(Next_Value_B_In_Exec));
  Multiplexer #(.Bits(8)) multiplexer_30 (
    .sel(Decoder_ROM_Output_16bit[8]), .in_0(Accumulator_A), .in_1(M), .out(Next_Value_C_In_Exec));
  Multiplexer #(.Selector_Bits(2), .Bits(8)) multiplexer_31 (
    .sel(Decoder_ROM_Output_16bit[11:10]), .in_0(Accumulator_A), .in_1(N), .in_2(Register_D_Minus_1),
    .in_3({8{1'b0}}), .out(Next_Value_D_In_Exec));
  and and_13 (GCD_Done_Update_A, State_Is_GCD_Loop, Compare_GCD_A_Equal_B);
  Multiplexer #(.Selector_Bits(2), .Bits(8)) multiplexer_32 (
    .sel(Decoder_ROM_Output_16bit[14:13]), .in_0(Instruction_Operand), .in_1(General_Register_C),
    .in_2(Stack_Pointer_Minus_1), .in_3(Stack_Pointer), .out(rRAM_Address_Exec));
  and and_14 (rRAM_Write_Enable_Exec, State_Is_Execute_Inst, Decoder_ROM_Output_16bit[12]);
  and and_15 (rRAM_Write_Enable_Fib, State_Is_Fibonacci_Loop, Fib_Write_Active);
  or or_17 (rRAM_Write_Enable_Loop5, rRAM_Write_Enable_Fib, SSUM_Write_Active);
  and and_16 (Start_GCD_Calculation, State_Is_Execute_Inst, Opcode_Is_GCD);
  and and_17 (Start_Fibonacci_Calculation, State_Is_Execute_Inst, Opcode_Is_FIB);
  and and_18 (Fib_Step_Clock_Enable, State_Is_Fibonacci_Loop, Fibonacci_Not_Finished);
  and and_19 (Fib_Write_Active, State_Is_Fibonacci_Loop, Fib_Counter_Is_Zero);
  and and_20 (Fibonacci_Finished_Flag, Fib_Write_Active, Fib_Write_Byte_Toggle);
  and and_21 (Start_SSUM_Calculation, State_Is_Execute_Inst, Opcode_Is_SSUM);
  and and_22 (SSUM_Step_Clock_Enable, State_Is_SSUM_Loop, SSUM_Not_Done_Sum);
  and and_23 (SSUM_Write_Active, State_Is_SSUM_Loop, SSUM_Done_Sum_Reg);
  and and_24 (SSUM_Finished_Flag, SSUM_Write_Active, SSUM_Write_Byte_Toggle);
  Comparator #(.Bits(8)) comparator_26 (.a(Stack_Pointer), .b({8{1'b0}}), .eq(SP_Is_Zero_Flag));  // open: gt, lt
  Comparator #(.Bits(8)) comparator_27 (.a(SSUM_Pointer_Reg), .b({8{1'b1}}), .eq(SSUM_Ptr_Is_FF_Flag));  // open: gt, lt
  and and_25 (Stack_Pointer_Enable_Exec, State_Is_Execute_Inst, Decoder_ROM_Output_16bit[15]);
  Multiplexer #(.Bits(8)) multiplexer_33 (
    .sel(Instruction_Opcode[0]), .in_0(Stack_Pointer_Minus_1), .in_1(Stack_Pointer_Plus_1),
    .out(Next_SP_In_Execute));
  and and_26 (Write_Enable_B_In_Exec, State_Is_Execute_Inst, Decoder_ROM_Output_16bit[5]);
  and and_27 (Write_Enable_C_In_Exec, State_Is_Execute_Inst, Decoder_ROM_Output_16bit[7]);
  and and_28 (Write_Enable_D_In_Exec, State_Is_Execute_Inst, Decoder_ROM_Output_16bit[9]);
  and and_29 (Write_Enable_A_In_Exec, State_Is_Execute_Inst, Decoder_ROM_Output_16bit[4]);
  and and_30 (pRAM_Address_Use_Operand, State_Is_Execute_Inst, Opcode_Is_PRAM_Access);
  Multiplexer #(.Bits(8)) multiplexer_34 (
    .sel(Fib_Write_Byte_Toggle), .in_0(8'ha), .in_1(8'hb), .out(rRAM_Address_Fib));
  or or_18 (rRAM_Write_Strobe, rRAM_Write_Enable_Exec, rRAM_Write_Enable_Loop5, State_Is_Clear_All);
  or or_19 (GCD_Clock_Enable, Start_GCD_Calculation, State_Is_GCD_Loop);
  Sub #(.Bits(8)) sub_4 (.a(GCD_Register_A), .b(GCD_Register_B), .c_i(1'b0), .s(GCD_A_Minus_B));  // open: c_o
  Sub #(.Bits(8)) sub_5 (.a(GCD_Register_B), .b(GCD_Register_A), .c_i(1'b0), .s(GCD_B_Minus_A));  // open: c_o
  Multiplexer #(.Bits(8)) multiplexer_35 (
    .sel(Opcode_Is_CALL), .in_0(Accumulator_A), .in_1(Program_Counter_Plus_1), .out(Exec_RAM_Data_In));
  or or_20 (Fib_Registers_Clock_Enable, Start_Fibonacci_Calculation, Fib_Step_Clock_Enable);
  not not_5 (Fibonacci_Not_Finished, Fib_Counter_Is_Zero);
  Register #(.Bits(1)) fib_step_reg (
    .D(Fib_Write_Active), .C(clk), .en(State_Is_Fibonacci_Loop), .Q(Fib_Write_Byte_Toggle));
  or or_21 (SSUM_Registers_Clock_Enable, Start_SSUM_Calculation, SSUM_Step_Clock_Enable);
  not not_6 (SSUM_Not_Done_Sum, SSUM_Done_Sum_Reg);
  or or_22 (SSUM_Toggle_Clock_Enable, Start_SSUM_Calculation, State_Is_SSUM_Loop);
  or or_23 (Loop5_Finished_Flag, Fibonacci_Finished_Flag, SSUM_Finished_Flag);
  Multiplexer #(.Bits(8)) multiplexer_36 (
    .sel(State_Is_Fibonacci_Loop), .in_0(rRAM_Address_Exec), .in_1(rRAM_Address_Fib),
    .out(rRAM_Address_Fib_Or_Exec));
  Multiplexer #(.Bits(8)) multiplexer_37 (
    .sel(Fib_Write_Byte_Toggle), .in_0(Fib_F0_High_Byte), .in_1(Fib_F0_Low_Byte), .out(Fib_RAM_Data_In));
  or or_24 (Write_Enable_B, Master_Clear_All_Pulse, Write_Enable_B_In_Exec);
  or or_25 (Write_Enable_C, Master_Clear_All_Pulse, Write_Enable_C_In_Exec);
  or or_26 (Write_Enable_D, Master_Clear_All_Pulse, Write_Enable_D_In_Exec);
  or or_27 (Write_Enable_A, Master_Clear_All_Pulse, Write_Enable_A_In_Exec, GCD_Done_Update_A);
  Multiplexer #(.Selector_Bits(3), .Bits(8)) multiplexer_38 (
    .sel(Decoder_ROM_Output_16bit[2:0]), .in_0(Instruction_Operand), .in_1(Accumulator_B),
    .in_2(General_Register_C), .in_3(General_Register_D), .in_4(Stack_Pointer), .in_5(\output ),
    .in_6(pRAM_Data_Low_8bit), .in_7(ALU_Result_Bus), .out(Next_Value_A_In_Exec));
  Sub #(.Bits(5)) sub_6 (.a(Fib_Down_Counter), .b(5'b00001), .c_i(1'b0), .s(Fib_Counter_Minus_1));  // open: c_o
  Add #(.Bits(16)) add_6 (
    .a({Fib_F0_High_Byte, Fib_F0_Low_Byte}), .b(Fib_Term_F1), .c_i(1'b0), .s(Fib_Sum_F0_Plus_F1));  // open: c_o
  Comparator #(.Bits(5)) comparator_28 (.a(Fib_Down_Counter), .b({5{1'b0}}), .eq(Fib_Counter_Is_Zero));  // open: gt, lt
  or or_28 (Stack_Pointer_Write_Enable, Reset_PC_and_SP_Pointers, Stack_Pointer_Enable_Exec);
  Multiplexer #(.Bits(8)) multiplexer_39 (
    .sel(Reset_PC_and_SP_Pointers), .in_0(Next_SP_In_Execute), .in_1({8{1'b0}}),
    .out(Next_Stack_Pointer_Value));
  Multiplexer #(.Bits(8)) multiplexer_40 (
    .sel(Compare_GCD_A_Greater_B), .in_0(GCD_Register_A), .in_1(GCD_A_Minus_B), .out(Next_GCD_A_Loop_Value));
  Multiplexer #(.Bits(8)) multiplexer_41 (
    .sel(Compare_GCD_A_Lesser_B), .in_0(GCD_Register_B), .in_1(GCD_B_Minus_A), .out(Next_GCD_B_Loop_Value));
  Add #(.Bits(8)) add_7 (.a(SSUM_Pointer_Reg), .b(8'h1), .c_i(1'b0), .s(SSUM_Ptr_Plus_1));  // open: c_o
  Add #(.Bits(16)) add_8 (
    .a(SSUM_Acc_16bit), .b({{8{1'b0}}, \output }), .c_i(1'b0), .s(SSUM_Acc_Plus_RAM));  // open: c_o
  Multiplexer #(.Bits(8)) multiplexer_42 (
    .sel(SSUM_Write_Byte_Toggle), .in_0(SSUM_Acc_16bit[15:8]), .in_1(SSUM_Acc_16bit[7:0]),
    .out(SSUM_RAM_Data_In));
  Multiplexer #(.Bits(8)) multiplexer_43 (
    .sel(SSUM_Write_Byte_Toggle), .in_0(8'hc), .in_1(8'hd), .out(SSUM_Write_Address));
  Multiplexer #(.Bits(8)) multiplexer_44 (
    .sel(SSUM_Done_Sum_Reg), .in_0(SSUM_Pointer_Reg), .in_1(SSUM_Write_Address), .out(rRAM_Address_SSUM));
  Multiplexer #(.Bits(8)) multiplexer_45 (
    .sel(Master_Clear_All_Pulse), .in_0(Next_Value_B_In_Exec), .in_1({8{1'b0}}), .out(Next_Value_B));
  Multiplexer #(.Bits(8)) multiplexer_46 (
    .sel(Master_Clear_All_Pulse), .in_0(Next_Value_C_In_Exec), .in_1({8{1'b0}}), .out(Next_Value_C));
  Multiplexer #(.Bits(8)) multiplexer_47 (
    .sel(Master_Clear_All_Pulse), .in_0(Next_Value_D_In_Exec), .in_1({8{1'b0}}), .out(Next_Value_D));
  Multiplexer #(.Bits(8)) multiplexer_48 (
    .sel(Master_Clear_All_Pulse), .in_0(Multiplexed_Value_A), .in_1({8{1'b0}}), .out(Next_Value_A));
  Multiplexer #(.Bits(8)) multiplexer_49 (
    .sel(State_Is_GCD_Loop), .in_0(Next_Value_A_In_Exec), .in_1(GCD_Register_A), .out(Multiplexed_Value_A));
  Multiplexer #(.Bits(8)) multiplexer_50 (
    .sel(pRAM_Address_Use_Operand), .in_0(Program_Counter), .in_1(Instruction_Operand),
    .out(pRAM_Address_Running));
  Multiplexer #(.Bits(8)) multiplexer_51 (
    .sel(Use_Loop_Counter_Select), .in_0(rRAM_Address_Running), .in_1({4'b0000, Loop_Counter_4bit}),
    .out(rRAM_Address_Pre_Reset));
  Multiplexer #(.Bits(8)) multiplexer_52 (
    .sel(State_Is_Fibonacci_Loop), .in_0(Exec_RAM_Data_In), .in_1(Fib_RAM_Data_In),
    .out(rRAM_Data_In_Fib_Or_Exec));
  Multiplexer #(.Bits(8)) multiplexer_53 (
    .sel(State_Is_SSUM_Loop), .in_0(rRAM_Address_Fib_Or_Exec), .in_1(rRAM_Address_SSUM),
    .out(rRAM_Address_Running));
  Multiplexer #(.Bits(5)) multiplexer_54 (
    .sel(State_Is_Fibonacci_Loop), .in_0(Accumulator_A[4:0]), .in_1(Fib_Counter_Minus_1),
    .out(Next_Fib_Counter_Value));
  Multiplexer #(.Bits(16)) multiplexer_55 (
    .sel(State_Is_Fibonacci_Loop), .in_0({16{1'b0}}), .in_1(Fib_Term_F1), .out(Next_Fib_F0_Value));
  Multiplexer #(.Bits(16)) multiplexer_56 (
    .sel(State_Is_Fibonacci_Loop), .in_0(16'h1), .in_1(Fib_Sum_F0_Plus_F1), .out(Next_Fib_F1_Value));
  Multiplexer #(.Bits(8)) multiplexer_57 (
    .sel(State_Is_GCD_Loop), .in_0(Accumulator_A), .in_1(Next_GCD_A_Loop_Value), .out(Next_GCD_A_Value));
  Multiplexer #(.Bits(8)) multiplexer_58 (
    .sel(State_Is_GCD_Loop), .in_0(Accumulator_B), .in_1(Next_GCD_B_Loop_Value), .out(Next_GCD_B_Value));
  Multiplexer #(.Bits(8)) multiplexer_59 (
    .sel(State_Is_SSUM_Loop), .in_0(Stack_Pointer), .in_1(SSUM_Ptr_Plus_1), .out(Next_SSUM_Ptr_Value));
  Multiplexer #(.Bits(16)) multiplexer_60 (
    .sel(State_Is_SSUM_Loop), .in_0({16{1'b0}}), .in_1(SSUM_Acc_Plus_RAM), .out(Next_SSUM_Acc_Value));
  Multiplexer #(.Bits(1)) multiplexer_61 (
    .sel(State_Is_SSUM_Loop), .in_0(SP_Is_Zero_Flag), .in_1(SSUM_Ptr_Is_FF_Flag), .out(Next_SSUM_Done_Value));
  Multiplexer #(.Bits(1)) multiplexer_62 (
    .sel(State_Is_SSUM_Loop), .in_0(1'b0), .in_1(SSUM_Write_Active), .out(Next_SSUM_Write_Toggle));
  Register #(.Bits(8)) SP (.D(Next_Stack_Pointer_Value), .C(clk), .en(Stack_Pointer_Write_Enable), .Q(Stack_Pointer));
  Register #(.Bits(8)) accB (.D(Next_Value_B), .C(clk), .en(Write_Enable_B), .Q(Accumulator_B));
  Register #(.Bits(8)) regC (.D(Next_Value_C), .C(clk), .en(Write_Enable_C), .Q(General_Register_C));
  Register #(.Bits(8)) regD (.D(Next_Value_D), .C(clk), .en(Write_Enable_D), .Q(General_Register_D));
  Register #(.Bits(8)) accA (.D(Next_Value_A), .C(clk), .en(Write_Enable_A), .Q(Accumulator_A));
  Multiplexer #(.Bits(8)) multiplexer_63 (
    .sel(progLoad), .in_0(pRAM_Address_Running), .in_1(Program_Load_Address), .out(pRAM_Address));
  Multiplexer #(.Bits(8)) multiplexer_64 (
    .sel(reset), .in_0(rRAM_Address_Pre_Reset), .in_1({8{1'b0}}), .out(rRAM_Address));
  Multiplexer #(.Bits(8)) multiplexer_65 (
    .sel(State_Is_Clear_All), .in_0(rRAM_Data_In_Running), .in_1({8{1'b0}}), .out(rRAM_Data_In));
  Multiplexer #(.Bits(8)) multiplexer_66 (
    .sel(State_Is_SSUM_Loop), .in_0(rRAM_Data_In_Fib_Or_Exec), .in_1(SSUM_RAM_Data_In),
    .out(rRAM_Data_In_Running));
  Register #(.Bits(8)) gcdA (.D(Next_GCD_A_Value), .C(clk), .en(GCD_Clock_Enable), .Q(GCD_Register_A));
  Register #(.Bits(8)) gcdB (.D(Next_GCD_B_Value), .C(clk), .en(GCD_Clock_Enable), .Q(GCD_Register_B));
  Register #(.Bits(5)) fibN (
    .D(Next_Fib_Counter_Value), .C(clk), .en(Fib_Registers_Clock_Enable), .Q(Fib_Down_Counter));
  Register #(.Bits(16)) fib0 (
    .D(Next_Fib_F0_Value), .C(clk), .en(Fib_Registers_Clock_Enable), .Q({Fib_F0_High_Byte, Fib_F0_Low_Byte}));
  Register #(.Bits(16)) fib1 (.D(Next_Fib_F1_Value), .C(clk), .en(Fib_Registers_Clock_Enable), .Q(Fib_Term_F1));
  Register #(.Bits(8)) ssumPtr (
    .D(Next_SSUM_Ptr_Value), .C(clk), .en(SSUM_Registers_Clock_Enable), .Q(SSUM_Pointer_Reg));
  Register #(.Bits(16)) ssumAcc (
    .D(Next_SSUM_Acc_Value), .C(clk), .en(SSUM_Registers_Clock_Enable), .Q(SSUM_Acc_16bit));
  Register #(.Bits(1)) ssumDone (
    .D(Next_SSUM_Done_Value), .C(clk), .en(SSUM_Registers_Clock_Enable), .Q(SSUM_Done_Sum_Reg));
  Register #(.Bits(1)) ssumStep (
    .D(Next_SSUM_Write_Toggle), .C(clk), .en(SSUM_Toggle_Clock_Enable), .Q(SSUM_Write_Byte_Toggle));

  // Other names for the same wires on the sheet: Accumulator_A_16bit_Doubled[15:0] = {Accumulator_A, Accumulator_A};
  //   Initial_Fib_N_5bit[4:0] = Accumulator_A[4:0]; Multiplier_Input_A_4bit[3:0] = Accumulator_A[3:0];
  //   Multiplier_Input_B_4bit[3:0] = Accumulator_B[3:0]; Rotate_Amount_From_B_3bit[2:0] = Accumulator_B[2:0];
  //   Shift_Amount_4bit[2:0] = Accumulator_B[2:0]; Shift_Amount_5bit[2:0] = Accumulator_B[2:0];
  //   Select_Input_Source_For_A[3:0] = Decoder_ROM_Output_16bit[3:0];
  //   Select_Input_Source_For_A_Bit3[2:0] = Decoder_ROM_Output_16bit[2:0];
  //   Instruction_Demands_Write_A = Decoder_ROM_Output_16bit[4];
  //   Instruction_Demands_Write_B = Decoder_ROM_Output_16bit[5];
  //   Select_Input_Source_For_B = Decoder_ROM_Output_16bit[6];
  //   Instruction_Demands_Write_C = Decoder_ROM_Output_16bit[7];
  //   Select_Input_Source_For_C = Decoder_ROM_Output_16bit[8];
  //   Instruction_Demands_Write_D = Decoder_ROM_Output_16bit[9];
  //   Select_Input_Source_For_D[1:0] = Decoder_ROM_Output_16bit[11:10];
  //   Memory_Write_Request = Decoder_ROM_Output_16bit[12];
  //   Select_rRAM_Address_Mode[1:0] = Decoder_ROM_Output_16bit[14:13];
  //   Stack_Operation_Active = Decoder_ROM_Output_16bit[15]; Fib_Term_F0[15:0] = {Fib_F0_High_Byte, Fib_F0_Low_Byte};
  //   Instruction_Register[13:0] = {Instruction_Opcode[5:4], Instruction_Bits_11_10, Instruction_Opcode[1:0], Instruction_Operand};
  //   Opcode_Bit_0 = Instruction_Opcode[0]; Opcode_Bits_1_0[1:0] = Instruction_Opcode[1:0];
  //   Opcode_Bits_3_0[3:0] = {Instruction_Bits_11_10, Instruction_Opcode[1:0]};
  //   Instruction_Opcode[3:2] = Instruction_Bits_11_10; Opcode_Bits_5_4[1:0] = Instruction_Opcode[5:4];
  //   Loop_Counter_8bit_Extended[3:0] = Loop_Counter_4bit; pRAM_Data_Out[7:0] = pRAM_Data_Low_8bit;
  //   Rotate_Left_Result[7:0] = Rotate_Left_16bit_Double[15:8];
  //   Rotate_Right_Result[7:0] = Rotate_Right_16bit_Double[7:0]; rRAM_Data_Out[7:0] = \output ;
  //   rRAM_Data_Out_16bit_ZeroExt[7:0] = \output ; SSUM_Acc_Low_Byte[7:0] = SSUM_Acc_16bit[7:0];
  //   SSUM_Acc_High_Byte[7:0] = SSUM_Acc_16bit[15:8]

  // Notes on the sheet:
  //   Testcase
  //   Group member
  //   6933076221 Natthatida Hutangkoon 
  //   6933277021 Sukrit Tongsri
  //   6933212221 Phuripong Deeted
  //   6933064721 Chanawat Chobtumkit
  //   Input
  //   Constants
  //   Branch & Program Counter (PC)
  //   RAM
  //   Output
  //   Decoder ROM
  //   contents of Decoder_ROM (hex, n*v repeats v):
  //   0,10,20,0,11,60,80,200,12,13,14,0,180,600,0,0,15,1000,16,0,2015
  //   ,3000,0,0,d000,e015,0,0,d000,e000,0,0,16*17,4*0,a00
  //   Registers & State Decoding
  //   Flags (CMP & isPrime)
  //   contents of Prime_ROM (hex, n*v repeats v):
  //   0,0,1,1,0,1,0,1,0,0,0,1,0,1,0,0,0,1,0,1,0,0,0,1,5*0,1,0,1,5*0
  //   ,1,0,0,0,1,0,1,0,0,0,1,5*0,1,5*0,1,0,1,5*0,1,0,0,0,1,0,1,5*0,1
  //   ,0,0,0,1,5*0,1,7*0,1,0,0,0,1,0,1,0,0,0,1,0,1,0,0,0,1,13*0,1,0,0,0
  //   ,1,5*0,1,0,1,9*0,1,0,1,5*0,1,5*0,1,0,0,0,1,5*0,1,5*0,1,0,1,9*0
  //   ,1,0,1,0,0,0,1,0,1,11*0,1,11*0,1,0,0,0,1,0,1,0,0,0,1,5*0,1,0,1
  //   ,9*0,1
  //   Next-State Logic & Control
  //   ALU (Arithmetic Logic Unit)
  //   Stack, Registers & RAM Mux
  //   Hardware Loops (GCD & FIB + SSUM)
endmodule

/* Test case 25_P12T02:
M N progIn reset progLoad start result clk valid done output
0 0 0 0 0 0 0 C x x x
0 0 0 1 0 0 0 C 0 0 x
repeat(20) 0 0 0 0 0 0 0 C 0 x x
0 0 511 0 1 0 0 C 0 x x
0 0 513 0 1 0 0 C 0 x x
0 0 15360 0 1 0 0 C 0 x x
0 0 4352 0 1 0 0 C 0 x x
0 0 257 0 1 0 0 C 0 x x
0 0 767 0 1 0 0 C 0 x x
0 0 15360 0 1 0 0 C 0 x x
0 0 4353 0 1 0 0 C 0 x x
0 0 384 0 1 0 0 C 0 x x
0 0 608 0 1 0 0 C 0 x x
0 0 15360 0 1 0 0 C 0 x x
0 0 4354 0 1 0 0 C 0 x x
0 0 477 0 1 0 0 C 0 x x
0 0 529 0 1 0 0 C 0 x x
0 0 15360 0 1 0 0 C 0 x x
0 0 4355 0 1 0 0 C 0 x x
0 0 506 0 1 0 0 C 0 x x
0 0 757 0 1 0 0 C 0 x x
0 0 15360 0 1 0 0 C 0 x x
0 0 4356 0 1 0 0 C 0 x x
0 0 1024 0 1 0 0 C 0 x x
0 0 4367 0 1 0 0 C 0 x x
0 0 16128 0 1 0 0 C 0 x x
0 0 0 0 0 1 0 C x 0 x
repeat(1821) 0 0 0 0 0 0 0 C x 0 x
0 0 0 0 0 0 0 C 1 0 x
0 0 0 0 0 0 1 C 1 0 1
0 0 0 0 0 0 0 C 1 0 1
0 0 0 0 0 0 0 C 1 0 32
0 0 0 0 0 0 0 C 1 0 17
0 0 0 0 0 0 0 C 1 0 5
repeat(10) 0 0 0 0 0 0 0 C 1 0 0
0 0 0 0 0 0 0 C 1 0 245
repeat(2) 0 0 0 0 0 0 0 C 1 1 x
*/

/* Test case 22_P09T02:
M N progIn reset progLoad start result clk valid done output
0 0 0 0 0 0 0 C x x x
0 0 0 1 0 0 0 C 0 0 x
repeat(20) 0 0 0 0 0 0 0 C 0 x x
0 0 435 0 1 0 0 C 0 x x
0 0 515 0 1 0 0 C 0 x x
0 0 11264 0 1 0 0 C 0 x x
0 0 4352 0 1 0 0 C 0 x x
0 0 435 0 1 0 0 C 0 x x
0 0 515 0 1 0 0 C 0 x x
0 0 11520 0 1 0 0 C 0 x x
0 0 4353 0 1 0 0 C 0 x x
0 0 435 0 1 0 0 C 0 x x
0 0 515 0 1 0 0 C 0 x x
0 0 11776 0 1 0 0 C 0 x x
0 0 4354 0 1 0 0 C 0 x x
0 0 435 0 1 0 0 C 0 x x
0 0 515 0 1 0 0 C 0 x x
0 0 12032 0 1 0 0 C 0 x x
0 0 4355 0 1 0 0 C 0 x x
0 0 435 0 1 0 0 C 0 x x
0 0 512 0 1 0 0 C 0 x x
0 0 11264 0 1 0 0 C 0 x x
0 0 4356 0 1 0 0 C 0 x x
0 0 435 0 1 0 0 C 0 x x
0 0 519 0 1 0 0 C 0 x x
0 0 12032 0 1 0 0 C 0 x x
0 0 4357 0 1 0 0 C 0 x x
0 0 435 0 1 0 0 C 0 x x
0 0 521 0 1 0 0 C 0 x x
0 0 11776 0 1 0 0 C 0 x x
0 0 4358 0 1 0 0 C 0 x x
0 0 435 0 1 0 0 C 0 x x
0 0 767 0 1 0 0 C 0 x x
0 0 11520 0 1 0 0 C 0 x x
0 0 4359 0 1 0 0 C 0 x x
0 0 16128 0 1 0 0 C 0 x x
0 0 0 0 0 1 0 C x 0 x
repeat(135) 0 0 0 0 0 0 0 C x 0 x
0 0 0 0 0 0 0 C 1 0 x
0 0 0 0 0 0 1 C 1 0 152
0 0 0 0 0 0 0 C 1 0 22
0 0 0 0 0 0 0 C 1 0 157
0 0 0 0 0 0 0 C 1 0 118
0 0 0 0 0 0 0 C 1 0 179
repeat(2) 0 0 0 0 0 0 0 C 1 0 103
0 0 0 0 0 0 0 C 1 0 1
repeat(8) 0 0 0 0 0 0 0 C 1 0 0
repeat(2) 0 0 0 0 0 0 0 C 1 1 x
*/

/* Test case 19_P06T02:
M N progIn reset progLoad start result clk valid done output
0 0 0 0 0 0 0 C x x x
0 0 0 1 0 0 0 C 0 0 x
repeat(20) 0 0 0 0 0 0 0 C 0 x x
0 0 3072 0 1 0 0 C 0 x x
0 0 3328 0 1 0 0 C 0 x x
0 0 2048 0 1 0 0 C 0 x x
0 0 4352 0 1 0 0 C 0 x x
0 0 2304 0 1 0 0 C 0 x x
0 0 4353 0 1 0 0 C 0 x x
0 0 2048 0 1 0 0 C 0 x x
0 0 1280 0 1 0 0 C 0 x x
0 0 2304 0 1 0 0 C 0 x x
0 0 8192 0 1 0 0 C 0 x x
0 0 4354 0 1 0 0 C 0 x x
0 0 16128 0 1 0 0 C 0 x x
3 4 0 0 0 1 0 C x 0 x
repeat(51) 3 4 0 0 0 0 0 C x 0 x
3 4 0 0 0 0 0 C 1 0 x
3 4 0 0 0 0 1 C 1 0 3
3 4 0 0 0 0 0 C 1 0 4
3 4 0 0 0 0 0 C 1 0 7
repeat(13) 3 4 0 0 0 0 0 C 1 0 0
repeat(2) 3 4 0 0 0 0 0 C 1 1 x
128 127 0 0 0 1 0 C x 0 x
repeat(51) 128 127 0 0 0 0 0 C x 0 x
128 127 0 0 0 0 0 C 1 0 x
128 127 0 0 0 0 1 C 1 0 128
128 127 0 0 0 0 0 C 1 0 127
128 127 0 0 0 0 0 C 1 0 255
repeat(13) 128 127 0 0 0 0 0 C 1 0 0
repeat(2) 128 127 0 0 0 0 0 C 1 1 x
*/

/* Test case 16_P03T02:
M N progIn reset progLoad start result clk valid done output
0 0 0 0 0 0 0 C x x x
0 0 0 1 0 0 0 C 0 0 x
repeat(20) 0 0 0 0 0 0 0 C 0 x x
0 0 4628 0 1 0 0 C 0 x x
0 0 4352 0 1 0 0 C 0 x x
0 0 4629 0 1 0 0 C 0 x x
0 0 4353 0 1 0 0 C 0 x x
0 0 4630 0 1 0 0 C 0 x x
0 0 4354 0 1 0 0 C 0 x x
0 0 4631 0 1 0 0 C 0 x x
0 0 4355 0 1 0 0 C 0 x x
0 0 4632 0 1 0 0 C 0 x x
0 0 4356 0 1 0 0 C 0 x x
0 0 4633 0 1 0 0 C 0 x x
0 0 4357 0 1 0 0 C 0 x x
0 0 4634 0 1 0 0 C 0 x x
0 0 4358 0 1 0 0 C 0 x x
0 0 4635 0 1 0 0 C 0 x x
0 0 4359 0 1 0 0 C 0 x x
0 0 16128 0 1 0 0 C 0 x x
repeat(3) 0 0 0 0 1 0 0 C 0 x x
0 0 16188 0 1 0 0 C 0 x x
0 0 16257 0 1 0 0 C 0 x x
0 0 16143 0 1 0 0 C 0 x x
0 0 16368 0 1 0 0 C 0 x x
0 0 16213 0 1 0 0 C 0 x x
0 0 16298 0 1 0 0 C 0 x x
0 0 16146 0 1 0 0 C 0 x x
0 0 16180 0 1 0 0 C 0 x x
0 0 0 0 0 1 0 C x 0 x
repeat(71) 0 0 0 0 0 0 0 C x 0 x
0 0 0 0 0 0 0 C 1 0 x
0 0 0 0 0 0 1 C 1 0 60
0 0 0 0 0 0 0 C 1 0 129
0 0 0 0 0 0 0 C 1 0 15
0 0 0 0 0 0 0 C 1 0 240
0 0 0 0 0 0 0 C 1 0 85
0 0 0 0 0 0 0 C 1 0 170
0 0 0 0 0 0 0 C 1 0 18
0 0 0 0 0 0 0 C 1 0 52
repeat(8) 0 0 0 0 0 0 0 C 1 0 0
repeat(2) 0 0 0 0 0 0 0 C 1 1 x
*/

/* Test case 12_P12T01:
M N progIn reset progLoad start result clk valid done output
0 0 0 0 0 0 0 0 x x x
0 0 0 0 0 0 0 1 x x x
0 0 0 1 0 0 0 0 x x x
0 0 0 1 0 0 0 1 0 0 x
0 0 0 0 0 0 0 0 0 x x
0 0 0 0 0 0 0 1 0 x x
0 0 0 0 0 0 0 0 0 x x
0 0 0 0 0 0 0 1 0 x x
0 0 0 0 0 0 0 0 0 x x
0 0 0 0 0 0 0 1 0 x x
0 0 0 0 0 0 0 0 0 x x
0 0 0 0 0 0 0 1 0 x x
0 0 0 0 0 0 0 0 0 x x
0 0 0 0 0 0 0 1 0 x x
0 0 0 0 0 0 0 0 0 x x
0 0 0 0 0 0 0 1 0 x x
0 0 0 0 0 0 0 0 0 x x
0 0 0 0 0 0 0 1 0 x x
0 0 0 0 0 0 0 0 0 x x
0 0 0 0 0 0 0 1 0 x x
0 0 0 0 0 0 0 0 0 x x
0 0 0 0 0 0 0 1 0 x x
0 0 0 0 0 0 0 0 0 x x
0 0 0 0 0 0 0 1 0 x x
0 0 0 0 0 0 0 0 0 x x
0 0 0 0 0 0 0 1 0 x x
0 0 0 0 0 0 0 0 0 x x
0 0 0 0 0 0 0 1 0 x x
0 0 0 0 0 0 0 0 0 x x
0 0 0 0 0 0 0 1 0 x x
0 0 0 0 0 0 0 0 0 x x
0 0 0 0 0 0 0 1 0 x x
0 0 0 0 0 0 0 0 0 x x
0 0 0 0 0 0 0 1 0 x x
0 0 0 0 0 0 0 0 0 x x
0 0 0 0 0 0 0 1 0 x x
0 0 0 0 0 0 0 0 0 x x
0 0 0 0 0 0 0 1 0 x x
0 0 0 0 0 0 0 0 0 x x
0 0 0 0 0 0 0 1 0 x x
0 0 0 0 0 0 0 0 0 x x
0 0 0 0 0 0 0 1 0 x x
0 0 0 0 0 0 0 0 0 x x
0 0 0 0 0 0 0 1 0 x x
0 0 268 0 1 0 0 0 0 x x
0 0 268 0 1 0 0 1 0 x x
0 0 530 0 1 0 0 0 0 x x
0 0 530 0 1 0 0 1 0 x x
0 0 15360 0 1 0 0 0 0 x x
0 0 15360 0 1 0 0 1 0 x x
0 0 4352 0 1 0 0 0 0 x x
0 0 4352 0 1 0 0 1 0 x x
0 0 356 0 1 0 0 0 0 x x
0 0 356 0 1 0 0 1 0 x x
0 0 587 0 1 0 0 0 0 x x
0 0 587 0 1 0 0 1 0 x x
0 0 15360 0 1 0 0 0 0 x x
0 0 15360 0 1 0 0 1 0 x x
0 0 4353 0 1 0 0 0 0 x x
0 0 4353 0 1 0 0 1 0 x x
0 0 273 0 1 0 0 0 0 x x
0 0 273 0 1 0 0 1 0 x x
0 0 517 0 1 0 0 0 0 x x
0 0 517 0 1 0 0 1 0 x x
0 0 15360 0 1 0 0 0 0 x x
0 0 15360 0 1 0 0 1 0 x x
0 0 4354 0 1 0 0 0 0 x x
0 0 4354 0 1 0 0 1 0 x x
0 0 304 0 1 0 0 0 0 x x
0 0 304 0 1 0 0 1 0 x x
0 0 560 0 1 0 0 0 0 x x
0 0 560 0 1 0 0 1 0 x x
0 0 15360 0 1 0 0 0 0 x x
0 0 15360 0 1 0 0 1 0 x x
0 0 4355 0 1 0 0 0 0 x x
0 0 4355 0 1 0 0 1 0 x x
0 0 1024 0 1 0 0 0 0 x x
0 0 1024 0 1 0 0 1 0 x x
0 0 4367 0 1 0 0 0 0 x x
0 0 4367 0 1 0 0 1 0 x x
0 0 16128 0 1 0 0 0 0 x x
0 0 16128 0 1 0 0 1 0 x x
0 0 0 0 0 1 0 0 x x x
0 0 0 0 0 1 0 1 x 0 x
0 0 0 0 0 0 0 0 x 0 x
0 0 0 0 0 0 0 1 x 0 x
0 0 0 0 0 0 0 0 x 0 x
0 0 0 0 0 0 0 1 x 0 x
0 0 0 0 0 0 0 0 x 0 x
0 0 0 0 0 0 0 1 x 0 x
0 0 0 0 0 0 0 0 x 0 x
0 0 0 0 0 0 0 1 x 0 x
0 0 0 0 0 0 0 0 x 0 x
0 0 0 0 0 0 0 1 x 0 x
0 0 0 0 0 0 0 0 x 0 x
0 0 0 0 0 0 0 1 x 0 x
0 0 0 0 0 0 0 0 x 0 x
0 0 0 0 0 0 0 1 x 0 x
0 0 0 0 0 0 0 0 x 0 x
0 0 0 0 0 0 0 1 x 0 x
0 0 0 0 0 0 0 0 x 0 x
0 0 0 0 0 0 0 1 x 0 x
0 0 0 0 0 0 0 0 x 0 x
0 0 0 0 0 0 0 1 x 0 x
0 0 0 0 0 0 0 0 x 0 x
0 0 0 0 0 0 0 1 x 0 x
0 0 0 0 0 0 0 0 x 0 x
0 0 0 0 0 0 0 1 x 0 x
0 0 0 0 0 0 0 0 x 0 x
0 0 0 0 0 0 0 1 x 0 x
0 0 0 0 0 0 0 0 x 0 x
0 0 0 0 0 0 0 1 x 0 x
0 0 0 0 0 0 0 0 x 0 x
0 0 0 0 0 0 0 1 x 0 x
0 0 0 0 0 0 0 0 x 0 x
0 0 0 0 0 0 0 1 x 0 x
0 0 0 0 0 0 0 0 x 0 x
0 0 0 0 0 0 0 1 x 0 x
0 0 0 0 0 0 0 0 x 0 x
0 0 0 0 0 0 0 1 x 0 x
0 0 0 0 0 0 0 0 x 0 x
0 0 0 0 0 0 0 1 x 0 x
0 0 0 0 0 0 0 0 x 0 x
0 0 0 0 0 0 0 1 x 0 x
0 0 0 0 0 0 0 0 x 0 x
0 0 0 0 0 0 0 1 x 0 x
0 0 0 0 0 0 0 0 x 0 x
0 0 0 0 0 0 0 1 x 0 x
0 0 0 0 0 0 0 0 x 0 x
0 0 0 0 0 0 0 1 x 0 x
0 0 0 0 0 0 0 0 x 0 x
0 0 0 0 0 0 0 1 x 0 x
0 0 0 0 0 0 0 0 x 0 x
0 0 0 0 0 0 0 1 x 0 x
0 0 0 0 0 0 0 0 x 0 x
0 0 0 0 0 0 0 1 x 0 x
0 0 0 0 0 0 0 0 x 0 x
0 0 0 0 0 0 0 1 x 0 x
0 0 0 0 0 0 0 0 x 0 x
0 0 0 0 0 0 0 1 x 0 x
0 0 0 0 0 0 0 0 x 0 x
0 0 0 0 0 0 0 1 x 0 x
0 0 0 0 0 0 0 0 x 0 x
0 0 0 0 0 0 0 1 x 0 x
0 0 0 0 0 0 0 0 x 0 x
0 0 0 0 0 0 0 1 x 0 x
0 0 0 0 0 0 0 0 x 0 x
0 0 0 0 0 0 0 1 x 0 x
0 0 0 0 0 0 0 0 x 0 x
0 0 0 0 0 0 0 1 x 0 x
0 0 0 0 0 0 0 0 x 0 x
0 0 0 0 0 0 0 1 x 0 x
0 0 0 0 0 0 0 0 x 0 x
0 0 0 0 0 0 0 1 x 0 x
0 0 0 0 0 0 0 0 x 0 x
0 0 0 0 0 0 0 1 x 0 x
0 0 0 0 0 0 0 0 x 0 x
0 0 0 0 0 0 0 1 x 0 x
0 0 0 0 0 0 0 0 x 0 x
0 0 0 0 0 0 0 1 x 0 x
0 0 0 0 0 0 0 0 x 0 x
0 0 0 0 0 0 0 1 x 0 x
0 0 0 0 0 0 0 0 x 0 x
0 0 0 0 0 0 0 1 x 0 x
0 0 0 0 0 0 0 0 x 0 x
0 0 0 0 0 0 0 1 x 0 x
0 0 0 0 0 0 0 0 x 0 x
0 0 0 0 0 0 0 1 x 0 x
0 0 0 0 0 0 0 0 x 0 x
0 0 0 0 0 0 0 1 x 0 x
0 0 0 0 0 0 0 0 x 0 x
0 0 0 0 0 0 0 1 x 0 x
0 0 0 0 0 0 0 0 x 0 x
0 0 0 0 0 0 0 1 x 0 x
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*/

/* Test case 09_P09T01:
M N progIn reset progLoad start result clk valid done output
0 0 0 0 0 0 0 0 x x x
0 0 0 0 0 0 0 1 x x x
0 0 0 1 0 0 0 0 x x x
0 0 0 1 0 0 0 1 0 0 x
0 0 0 0 0 0 0 0 0 x x
0 0 0 0 0 0 0 1 0 x x
0 0 0 0 0 0 0 0 0 x x
0 0 0 0 0 0 0 1 0 x x
0 0 0 0 0 0 0 0 0 x x
0 0 0 0 0 0 0 1 0 x x
0 0 0 0 0 0 0 0 0 x x
0 0 0 0 0 0 0 1 0 x x
0 0 0 0 0 0 0 0 0 x x
0 0 0 0 0 0 0 1 0 x x
0 0 0 0 0 0 0 0 0 x x
0 0 0 0 0 0 0 1 0 x x
0 0 0 0 0 0 0 0 0 x x
0 0 0 0 0 0 0 1 0 x x
0 0 0 0 0 0 0 0 0 x x
0 0 0 0 0 0 0 1 0 x x
0 0 0 0 0 0 0 0 0 x x
0 0 0 0 0 0 0 1 0 x x
0 0 0 0 0 0 0 0 0 x x
0 0 0 0 0 0 0 1 0 x x
0 0 0 0 0 0 0 0 0 x x
0 0 0 0 0 0 0 1 0 x x
0 0 0 0 0 0 0 0 0 x x
0 0 0 0 0 0 0 1 0 x x
0 0 0 0 0 0 0 0 0 x x
0 0 0 0 0 0 0 1 0 x x
0 0 0 0 0 0 0 0 0 x x
0 0 0 0 0 0 0 1 0 x x
0 0 0 0 0 0 0 0 0 x x
0 0 0 0 0 0 0 1 0 x x
0 0 0 0 0 0 0 0 0 x x
0 0 0 0 0 0 0 1 0 x x
0 0 0 0 0 0 0 0 0 x x
0 0 0 0 0 0 0 1 0 x x
0 0 0 0 0 0 0 0 0 x x
0 0 0 0 0 0 0 1 0 x x
0 0 0 0 0 0 0 0 0 x x
0 0 0 0 0 0 0 1 0 x x
0 0 0 0 0 0 0 0 0 x x
0 0 0 0 0 0 0 1 0 x x
0 0 458 0 1 0 0 0 0 x x
0 0 458 0 1 0 0 1 0 x x
0 0 607 0 1 0 0 0 0 x x
0 0 607 0 1 0 0 1 0 x x
0 0 10240 0 1 0 0 0 0 x x
0 0 10240 0 1 0 0 1 0 x x
0 0 4352 0 1 0 0 0 0 x x
0 0 4352 0 1 0 0 1 0 x x
0 0 458 0 1 0 0 0 0 x x
0 0 458 0 1 0 0 1 0 x x
0 0 10496 0 1 0 0 0 0 x x
0 0 10496 0 1 0 0 1 0 x x
0 0 4353 0 1 0 0 0 0 x x
0 0 4353 0 1 0 0 1 0 x x
0 0 458 0 1 0 0 0 0 x x
0 0 458 0 1 0 0 1 0 x x
0 0 10752 0 1 0 0 0 0 x x
0 0 10752 0 1 0 0 1 0 x x
0 0 4354 0 1 0 0 0 0 x x
0 0 4354 0 1 0 0 1 0 x x
0 0 458 0 1 0 0 0 0 x x
0 0 458 0 1 0 0 1 0 x x
0 0 11008 0 1 0 0 0 0 x x
0 0 11008 0 1 0 0 1 0 x x
0 0 4355 0 1 0 0 0 0 x x
0 0 4355 0 1 0 0 1 0 x x
0 0 16128 0 1 0 0 0 0 x x
0 0 16128 0 1 0 0 1 0 x x
0 0 0 0 0 1 0 0 x x x
0 0 0 0 0 1 0 1 x 0 x
0 0 0 0 0 0 0 0 x 0 x
0 0 0 0 0 0 0 1 x 0 x
0 0 0 0 0 0 0 0 x 0 x
0 0 0 0 0 0 0 1 x 0 x
0 0 0 0 0 0 0 0 x 0 x
0 0 0 0 0 0 0 1 x 0 x
0 0 0 0 0 0 0 0 x 0 x
0 0 0 0 0 0 0 1 x 0 x
0 0 0 0 0 0 0 0 x 0 x
0 0 0 0 0 0 0 1 x 0 x
0 0 0 0 0 0 0 0 x 0 x
0 0 0 0 0 0 0 1 x 0 x
0 0 0 0 0 0 0 0 x 0 x
0 0 0 0 0 0 0 1 x 0 x
0 0 0 0 0 0 0 0 x 0 x
0 0 0 0 0 0 0 1 x 0 x
0 0 0 0 0 0 0 0 x 0 x
0 0 0 0 0 0 0 1 x 0 x
0 0 0 0 0 0 0 0 x 0 x
0 0 0 0 0 0 0 1 x 0 x
0 0 0 0 0 0 0 0 x 0 x
0 0 0 0 0 0 0 1 x 0 x
0 0 0 0 0 0 0 0 x 0 x
0 0 0 0 0 0 0 1 x 0 x
0 0 0 0 0 0 0 0 x 0 x
0 0 0 0 0 0 0 1 x 0 x
0 0 0 0 0 0 0 0 x 0 x
0 0 0 0 0 0 0 1 x 0 x
0 0 0 0 0 0 0 0 x 0 x
0 0 0 0 0 0 0 1 x 0 x
0 0 0 0 0 0 0 0 x 0 x
0 0 0 0 0 0 0 1 x 0 x
0 0 0 0 0 0 0 0 x 0 x
0 0 0 0 0 0 0 1 x 0 x
0 0 0 0 0 0 0 0 x 0 x
0 0 0 0 0 0 0 1 x 0 x
0 0 0 0 0 0 0 0 x 0 x
0 0 0 0 0 0 0 1 x 0 x
0 0 0 0 0 0 0 0 x 0 x
0 0 0 0 0 0 0 1 x 0 x
0 0 0 0 0 0 0 0 x 0 x
0 0 0 0 0 0 0 1 x 0 x
0 0 0 0 0 0 0 0 x 0 x
0 0 0 0 0 0 0 1 x 0 x
0 0 0 0 0 0 0 0 x 0 x
0 0 0 0 0 0 0 1 x 0 x
0 0 0 0 0 0 0 0 x 0 x
0 0 0 0 0 0 0 1 x 0 x
0 0 0 0 0 0 0 0 x 0 x
0 0 0 0 0 0 0 1 x 0 x
0 0 0 0 0 0 0 0 x 0 x
0 0 0 0 0 0 0 1 x 0 x
0 0 0 0 0 0 0 0 x 0 x
0 0 0 0 0 0 0 1 x 0 x
0 0 0 0 0 0 0 0 x 0 x
0 0 0 0 0 0 0 1 x 0 x
0 0 0 0 0 0 0 0 x 0 x
0 0 0 0 0 0 0 1 x 0 x
0 0 0 0 0 0 0 0 x 0 x
0 0 0 0 0 0 0 1 x 0 x
0 0 0 0 0 0 0 0 x 0 x
0 0 0 0 0 0 0 1 x 0 x
0 0 0 0 0 0 0 0 x 0 x
0 0 0 0 0 0 0 1 x 0 x
0 0 0 0 0 0 0 0 x 0 x
0 0 0 0 0 0 0 1 x 0 x
0 0 0 0 0 0 0 0 x 0 x
0 0 0 0 0 0 0 1 x 0 x
0 0 0 0 0 0 0 0 x 0 x
0 0 0 0 0 0 0 1 x 0 x
0 0 0 0 0 0 0 0 x 0 x
0 0 0 0 0 0 0 1 x 0 x
0 0 0 0 0 0 0 0 x 0 x
0 0 0 0 0 0 0 1 x 0 x
0 0 0 0 0 0 0 0 x 0 x
0 0 0 0 0 0 0 1 x 0 x
0 0 0 0 0 0 0 0 x 0 x
0 0 0 0 0 0 0 1 x 0 x
0 0 0 0 0 0 0 0 x 0 x
0 0 0 0 0 0 0 1 x 0 x
0 0 0 0 0 0 0 0 x 0 x
0 0 0 0 0 0 0 1 x 0 x
0 0 0 0 0 0 0 0 x 0 x
0 0 0 0 0 0 0 1 x 0 x
0 0 0 0 0 0 0 0 x 0 x
0 0 0 0 0 0 0 1 x 0 x
0 0 0 0 0 0 0 0 x 0 x
0 0 0 0 0 0 0 1 x 0 x
0 0 0 0 0 0 0 0 x 0 x
0 0 0 0 0 0 0 1 x 0 x
0 0 0 0 0 0 0 0 x 0 x
0 0 0 0 0 0 0 1 x 0 x
0 0 0 0 0 0 0 0 x 0 x
0 0 0 0 0 0 0 1 x 0 x
0 0 0 0 0 0 0 0 x 0 x
0 0 0 0 0 0 0 1 x 0 x
0 0 0 0 0 0 0 0 x 0 x
0 0 0 0 0 0 0 1 x 0 x
0 0 0 0 0 0 0 0 x 0 x
0 0 0 0 0 0 0 1 x 0 x
0 0 0 0 0 0 0 0 x 0 x
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*/

/* Test case 06_P06T01:
M N progIn reset progLoad start result clk valid done output
0 0 0 0 0 0 0 0 x x x
0 0 0 0 0 0 0 1 x x x
0 0 0 1 0 0 0 0 x x x
0 0 0 1 0 0 0 1 0 0 x
0 0 0 0 0 0 0 0 0 x x
0 0 0 0 0 0 0 1 0 x x
0 0 0 0 0 0 0 0 0 x x
0 0 0 0 0 0 0 1 0 x x
0 0 0 0 0 0 0 0 0 x x
0 0 0 0 0 0 0 1 0 x x
0 0 0 0 0 0 0 0 0 x x
0 0 0 0 0 0 0 1 0 x x
0 0 0 0 0 0 0 0 0 x x
0 0 0 0 0 0 0 1 0 x x
0 0 0 0 0 0 0 0 0 x x
0 0 0 0 0 0 0 1 0 x x
0 0 0 0 0 0 0 0 0 x x
0 0 0 0 0 0 0 1 0 x x
0 0 0 0 0 0 0 0 0 x x
0 0 0 0 0 0 0 1 0 x x
0 0 0 0 0 0 0 0 0 x x
0 0 0 0 0 0 0 1 0 x x
0 0 0 0 0 0 0 0 0 x x
0 0 0 0 0 0 0 1 0 x x
0 0 0 0 0 0 0 0 0 x x
0 0 0 0 0 0 0 1 0 x x
0 0 0 0 0 0 0 0 0 x x
0 0 0 0 0 0 0 1 0 x x
0 0 0 0 0 0 0 0 0 x x
0 0 0 0 0 0 0 1 0 x x
0 0 0 0 0 0 0 0 0 x x
0 0 0 0 0 0 0 1 0 x x
0 0 0 0 0 0 0 0 0 x x
0 0 0 0 0 0 0 1 0 x x
0 0 0 0 0 0 0 0 0 x x
0 0 0 0 0 0 0 1 0 x x
0 0 0 0 0 0 0 0 0 x x
0 0 0 0 0 0 0 1 0 x x
0 0 0 0 0 0 0 0 0 x x
0 0 0 0 0 0 0 1 0 x x
0 0 0 0 0 0 0 0 0 x x
0 0 0 0 0 0 0 1 0 x x
0 0 0 0 0 0 0 0 0 x x
0 0 0 0 0 0 0 1 0 x x
0 0 3072 0 1 0 0 0 0 x x
0 0 3072 0 1 0 0 1 0 x x
0 0 3328 0 1 0 0 0 0 x x
0 0 3328 0 1 0 0 1 0 x x
0 0 2048 0 1 0 0 0 0 x x
0 0 2048 0 1 0 0 1 0 x x
0 0 4352 0 1 0 0 0 0 x x
0 0 4352 0 1 0 0 1 0 x x
0 0 2304 0 1 0 0 0 0 x x
0 0 2304 0 1 0 0 1 0 x x
0 0 4353 0 1 0 0 0 0 x x
0 0 4353 0 1 0 0 1 0 x x
0 0 2048 0 1 0 0 0 0 x x
0 0 2048 0 1 0 0 1 0 x x
0 0 1280 0 1 0 0 0 0 x x
0 0 1280 0 1 0 0 1 0 x x
0 0 2304 0 1 0 0 0 0 x x
0 0 2304 0 1 0 0 1 0 x x
0 0 8192 0 1 0 0 0 0 x x
0 0 8192 0 1 0 0 1 0 x x
0 0 4354 0 1 0 0 0 0 x x
0 0 4354 0 1 0 0 1 0 x x
0 0 16128 0 1 0 0 0 0 x x
0 0 16128 0 1 0 0 1 0 x x
18 52 0 0 0 1 0 0 x x x
18 52 0 0 0 1 0 1 x 0 x
18 52 0 0 0 0 0 0 x 0 x
18 52 0 0 0 0 0 1 x 0 x
18 52 0 0 0 0 0 0 x 0 x
18 52 0 0 0 0 0 1 x 0 x
18 52 0 0 0 0 0 0 x 0 x
18 52 0 0 0 0 0 1 x 0 x
18 52 0 0 0 0 0 0 x 0 x
18 52 0 0 0 0 0 1 x 0 x
18 52 0 0 0 0 0 0 x 0 x
18 52 0 0 0 0 0 1 x 0 x
18 52 0 0 0 0 0 0 x 0 x
18 52 0 0 0 0 0 1 x 0 x
18 52 0 0 0 0 0 0 x 0 x
18 52 0 0 0 0 0 1 x 0 x
18 52 0 0 0 0 0 0 x 0 x
18 52 0 0 0 0 0 1 x 0 x
18 52 0 0 0 0 0 0 x 0 x
18 52 0 0 0 0 0 1 x 0 x
18 52 0 0 0 0 0 0 x 0 x
18 52 0 0 0 0 0 1 x 0 x
18 52 0 0 0 0 0 0 x 0 x
18 52 0 0 0 0 0 1 x 0 x
18 52 0 0 0 0 0 0 x 0 x
18 52 0 0 0 0 0 1 x 0 x
18 52 0 0 0 0 0 0 x 0 x
18 52 0 0 0 0 0 1 x 0 x
18 52 0 0 0 0 0 0 x 0 x
18 52 0 0 0 0 0 1 x 0 x
18 52 0 0 0 0 0 0 x 0 x
18 52 0 0 0 0 0 1 x 0 x
18 52 0 0 0 0 0 0 x 0 x
18 52 0 0 0 0 0 1 x 0 x
18 52 0 0 0 0 0 0 x 0 x
18 52 0 0 0 0 0 1 x 0 x
18 52 0 0 0 0 0 0 x 0 x
18 52 0 0 0 0 0 1 x 0 x
18 52 0 0 0 0 0 0 x 0 x
18 52 0 0 0 0 0 1 x 0 x
18 52 0 0 0 0 0 0 x 0 x
18 52 0 0 0 0 0 1 x 0 x
18 52 0 0 0 0 0 0 x 0 x
18 52 0 0 0 0 0 1 x 0 x
18 52 0 0 0 0 0 0 x 0 x
18 52 0 0 0 0 0 1 x 0 x
18 52 0 0 0 0 0 0 x 0 x
18 52 0 0 0 0 0 1 x 0 x
18 52 0 0 0 0 0 0 x 0 x
18 52 0 0 0 0 0 1 x 0 x
18 52 0 0 0 0 0 0 x 0 x
18 52 0 0 0 0 0 1 x 0 x
18 52 0 0 0 0 0 0 x 0 x
18 52 0 0 0 0 0 1 x 0 x
18 52 0 0 0 0 0 0 x 0 x
18 52 0 0 0 0 0 1 x 0 x
18 52 0 0 0 0 0 0 x 0 x
18 52 0 0 0 0 0 1 x 0 x
18 52 0 0 0 0 0 0 x 0 x
18 52 0 0 0 0 0 1 x 0 x
18 52 0 0 0 0 0 0 x 0 x
18 52 0 0 0 0 0 1 x 0 x
18 52 0 0 0 0 0 0 x 0 x
18 52 0 0 0 0 0 1 x 0 x
18 52 0 0 0 0 0 0 x 0 x
18 52 0 0 0 0 0 1 x 0 x
18 52 0 0 0 0 0 0 x 0 x
18 52 0 0 0 0 0 1 x 0 x
18 52 0 0 0 0 0 0 x 0 x
18 52 0 0 0 0 0 1 x 0 x
18 52 0 0 0 0 0 0 x 0 x
18 52 0 0 0 0 0 1 x 0 x
18 52 0 0 0 0 0 0 x 0 x
18 52 0 0 0 0 0 1 x 0 x
18 52 0 0 0 0 0 0 x 0 x
18 52 0 0 0 0 0 1 x 0 x
18 52 0 0 0 0 0 0 x 0 x
18 52 0 0 0 0 0 1 x 0 x
18 52 0 0 0 0 0 0 x 0 x
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*/

/* Test case 03_P03T01:
M N progIn reset progLoad start result clk valid done output
0 0 0 0 0 0 0 0 x x x
0 0 0 0 0 0 0 1 x x x
0 0 0 1 0 0 0 0 x x x
0 0 0 1 0 0 0 1 0 0 x
0 0 0 0 0 0 0 0 0 x x
0 0 0 0 0 0 0 1 0 x x
0 0 0 0 0 0 0 0 0 x x
0 0 0 0 0 0 0 1 0 x x
0 0 0 0 0 0 0 0 0 x x
0 0 0 0 0 0 0 1 0 x x
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*/

/* Test case 24_P11T02:
M N progIn reset progLoad start result clk valid done output
0 0 0 0 0 0 0 C x x x
0 0 0 1 0 0 0 C 0 0 x
repeat(20) 0 0 0 0 0 0 0 C 0 x x
0 0 256 0 1 0 0 C 0 x x
0 0 1536 0 1 0 0 C 0 x x
0 0 259 0 1 0 0 C 0 x x
0 0 1792 0 1 0 0 C 0 x x
0 0 2304 0 1 0 0 C 0 x x
0 0 6144 0 1 0 0 C 0 x x
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*/

/* Test case 21_P08T02:
M N progIn reset progLoad start result clk valid done output
0 0 0 0 0 0 0 C x x x
0 0 0 1 0 0 0 C 0 0 x
repeat(20) 0 0 0 0 0 0 0 C 0 x x
0 0 456 0 1 0 0 C 0 x x
0 0 519 0 1 0 0 C 0 x x
0 0 9216 0 1 0 0 C 0 x x
0 0 4352 0 1 0 0 C 0 x x
0 0 456 0 1 0 0 C 0 x x
0 0 9472 0 1 0 0 C 0 x x
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*/

/* Test case 18_P05T02:
M N progIn reset progLoad start result clk valid done output
0 0 0 0 0 0 0 C x x x
0 0 0 1 0 0 0 C 0 0 x
repeat(20) 0 0 0 0 0 0 0 C 0 x x
0 0 260 0 1 0 0 C 0 x x
0 0 516 0 1 0 0 C 0 x x
0 0 14336 0 1 0 0 C 0 x x
0 0 14592 0 1 0 0 C 0 x x
0 0 12569 0 1 0 0 C 0 x x
0 0 257 0 1 0 0 C 0 x x
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*/

/* Test case 15_P02T02:
M N progIn reset progLoad start result clk valid done output
0 0 0 0 0 0 0 C x x x
0 0 0 1 0 0 0 C 0 0 x
repeat(20) 0 0 0 0 0 0 0 C 0 x x
0 0 496 0 1 0 0 C 0 x x
0 0 517 0 1 0 0 C 0 x x
0 0 14336 0 1 0 0 C 0 x x
0 0 13061 0 1 0 0 C 0 x x
0 0 256 0 1 0 0 C 0 x x
0 0 4352 0 1 0 0 C 0 x x
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*/

/* Test case 11_P11T01:
M N progIn reset progLoad start result clk valid done output
0 0 0 0 0 0 0 0 x x x
0 0 0 0 0 0 0 1 x x x
0 0 0 1 0 0 0 0 x x x
0 0 0 1 0 0 0 1 0 0 x
0 0 0 0 0 0 0 0 0 x x
0 0 0 0 0 0 0 1 0 x x
0 0 0 0 0 0 0 0 0 x x
0 0 0 0 0 0 0 1 0 x x
0 0 0 0 0 0 0 0 0 x x
0 0 0 0 0 0 0 1 0 x x
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*/

/* Test case 08_P08T01:
M N progIn reset progLoad start result clk valid done output
0 0 0 0 0 0 0 0 x x x
0 0 0 0 0 0 0 1 x x x
0 0 0 1 0 0 0 0 x x x
0 0 0 1 0 0 0 1 0 0 x
0 0 0 0 0 0 0 0 0 x x
0 0 0 0 0 0 0 1 0 x x
0 0 0 0 0 0 0 0 0 x x
0 0 0 0 0 0 0 1 0 x x
0 0 0 0 0 0 0 0 0 x x
0 0 0 0 0 0 0 1 0 x x
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*/

/* Test case 05_P05T01:
M N progIn reset progLoad start result clk valid done output
0 0 0 0 0 0 0 0 x x x
0 0 0 0 0 0 0 1 x x x
0 0 0 1 0 0 0 0 x x x
0 0 0 1 0 0 0 1 0 0 x
0 0 0 0 0 0 0 0 0 x x
0 0 0 0 0 0 0 1 0 x x
0 0 0 0 0 0 0 0 0 x x
0 0 0 0 0 0 0 1 0 x x
0 0 0 0 0 0 0 0 0 x x
0 0 0 0 0 0 0 1 0 x x
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*/

/* Test case 02_P02T01:
M N progIn reset progLoad start result clk valid done output
0 0 0 0 0 0 0 0 x x x
0 0 0 0 0 0 0 1 x x x
0 0 0 1 0 0 0 0 x x x
0 0 0 1 0 0 0 1 0 0 x
0 0 0 0 0 0 0 0 0 x x
0 0 0 0 0 0 0 1 0 x x
0 0 0 0 0 0 0 0 0 x x
0 0 0 0 0 0 0 1 0 x x
0 0 0 0 0 0 0 0 0 x x
0 0 0 0 0 0 0 1 0 x x
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*/

/* Test case 26_P13T02:
M N progIn reset progLoad start result clk valid done output
0 0 0 0 0 0 0 C x x x
0 0 0 1 0 0 0 C 0 0 x
repeat(20) 0 0 0 0 0 0 0 C 0 x x
0 0 280 0 1 0 0 C 0 x x
0 0 15616 0 1 0 0 C 0 x x
0 0 4106 0 1 0 0 C 0 x x
0 0 4352 0 1 0 0 C 0 x x
0 0 4107 0 1 0 0 C 0 x x
0 0 4353 0 1 0 0 C 0 x x
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*/

/* Test case 23_P10T02:
M N progIn reset progLoad start result clk valid done output
0 0 0 0 0 0 0 C x x x
0 0 0 1 0 0 0 C 0 0 x
repeat(20) 0 0 0 0 0 0 0 C 0 x x
0 0 264 0 1 0 0 C 0 x x
0 0 1792 0 1 0 0 C 0 x x
0 0 273 0 1 0 0 C 0 x x
0 0 6144 0 1 0 0 C 0 x x
0 0 529 0 1 0 0 C 0 x x
0 0 8192 0 1 0 0 C 0 x x
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*/

/* Test case 20_P07T02:
M N progIn reset progLoad start result clk valid done output
0 0 0 0 0 0 0 C x x x
0 0 0 1 0 0 0 C 0 0 x
repeat(20) 0 0 0 0 0 0 0 C 0 x x
0 0 320 0 1 0 0 C 0 x x
0 0 1536 0 1 0 0 C 0 x x
0 0 264 0 1 0 0 C 0 x x
0 0 1792 0 1 0 0 C 0 x x
0 0 259 0 1 0 0 C 0 x x
0 0 5376 0 1 0 0 C 0 x x
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*/

/* Test case 17_P04T02:
M N progIn reset progLoad start result clk valid done output
0 0 0 0 0 0 0 C x x x
0 0 0 1 0 0 0 C 0 0 x
repeat(20) 0 0 0 0 0 0 0 C 0 x x
0 0 256 0 1 0 0 C 0 x x
0 0 14592 0 1 0 0 C 0 x x
0 0 256 0 1 0 0 C 0 x x
0 0 12549 0 1 0 0 C 0 x x
0 0 12294 0 1 0 0 C 0 x x
0 0 257 0 1 0 0 C 0 x x
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*/

/* Test case 14_P01T02:
M N progIn reset progLoad start result clk valid done output
0 0 0 0 0 0 0 C x x x
0 0 0 1 0 0 0 C 0 0 x
repeat(20) 0 0 0 0 0 0 0 C 0 x x
0 0 346 0 1 0 0 C 0 x x
0 0 4352 0 1 0 0 C 0 x x
0 0 677 0 1 0 0 C 0 x x
0 0 1024 0 1 0 0 C 0 x x
0 0 4367 0 1 0 0 C 0 x x
0 0 375 0 1 0 0 C 0 x x
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*/

/* Test case 13_P13T01:
M N progIn reset progLoad start result clk valid done output
0 0 0 0 0 0 0 0 x x x
0 0 0 0 0 0 0 1 x x x
0 0 0 1 0 0 0 0 x x x
0 0 0 1 0 0 0 1 0 0 x
0 0 0 0 0 0 0 0 0 x x
0 0 0 0 0 0 0 1 0 x x
0 0 0 0 0 0 0 0 0 x x
0 0 0 0 0 0 0 1 0 x x
0 0 0 0 0 0 0 0 0 x x
0 0 0 0 0 0 0 1 0 x x
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*/

/* Test case 10_P10T01:
M N progIn reset progLoad start result clk valid done output
0 0 0 0 0 0 0 0 x x x
0 0 0 0 0 0 0 1 x x x
0 0 0 1 0 0 0 0 x x x
0 0 0 1 0 0 0 1 0 0 x
0 0 0 0 0 0 0 0 0 x x
0 0 0 0 0 0 0 1 0 x x
0 0 0 0 0 0 0 0 0 x x
0 0 0 0 0 0 0 1 0 x x
0 0 0 0 0 0 0 0 0 x x
0 0 0 0 0 0 0 1 0 x x
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*/

/* Test case 07_P07T01:
M N progIn reset progLoad start result clk valid done output
0 0 0 0 0 0 0 0 x x x
0 0 0 0 0 0 0 1 x x x
0 0 0 1 0 0 0 0 x x x
0 0 0 1 0 0 0 1 0 0 x
0 0 0 0 0 0 0 0 0 x x
0 0 0 0 0 0 0 1 0 x x
0 0 0 0 0 0 0 0 0 x x
0 0 0 0 0 0 0 1 0 x x
0 0 0 0 0 0 0 0 0 x x
0 0 0 0 0 0 0 1 0 x x
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*/

/* Test case 04_P04T01:
M N progIn reset progLoad start result clk valid done output
0 0 0 0 0 0 0 0 x x x
0 0 0 0 0 0 0 1 x x x
0 0 0 1 0 0 0 0 x x x
0 0 0 1 0 0 0 1 0 0 x
0 0 0 0 0 0 0 0 0 x x
0 0 0 0 0 0 0 1 0 x x
0 0 0 0 0 0 0 0 0 x x
0 0 0 0 0 0 0 1 0 x x
0 0 0 0 0 0 0 0 0 x x
0 0 0 0 0 0 0 1 0 x x
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*/

/* Test case 01_P01T01:
M N progIn reset progLoad start result clk valid done output
0 0 0 0 0 0 0 0 x x x
0 0 0 0 0 0 0 1 x x x
0 0 0 1 0 0 0 0 x x x
0 0 0 1 0 0 0 1 0 0 x
0 0 0 0 0 0 0 0 0 x x
0 0 0 0 0 0 0 1 0 x x
0 0 0 0 0 0 0 0 0 x x
0 0 0 0 0 0 0 1 0 x x
0 0 0 0 0 0 0 0 0 x x
0 0 0 0 0 0 0 1 0 x x
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*/
