// Digital circuit MiniCPU_Complete(2).dig as structural Verilog
module MiniCPU_Complete_2 (
  input  [7:0] M,
  input  [7:0] N,
  input  [13:0] progIn,
  input  reset,
  input  progLoad,
  input  start,
  input  result,
  input  clk,
  output valid,
  output done,
  output [7:0] \output 
);

  wire a_en, a_en_ex, b_en, b_en_ex, br_cond, c_en, c_en_ex, clr_all, clr_done_stop, clr_pc_sp, cmp_eq,
       cmp_gr, cmp_ls, cnt4_is15, d_en, d_en_ex, dec_a_we, dec_b_sel, dec_b_we, dec_c_sel, dec_c_we,
       dec_d_we, done_d, done_no_rst, eq, eq_d, eq_en, eq_target, eq_we_ex, fib_done, fib_init, fib_n_is0,
       fib_not_done, fib_regs_en, fib_step, fib_step_en, fib_we_active, flags_update_op, gcd_done_a, gcd_en,
       gcd_eq, gcd_gt, gcd_init, gcd_lt, gr, gr_d, gr_en, gr_we_ex, hold_done, is_clear, is_ctrl_grp,
       is_exec, is_fetch, is_fib, is_gcd, is_idle, is_out, is_stop, is_sub_00, keep_done_stop, ls, ls_d,
       ns_eq6, ns_gt6, op_is_cmp, op_is_djnz, op_is_fib, op_is_gcd, op_is_pram, op_is_prime, op_is_stop,
       pc_en, pc_en_ex, pc_en_fib, pc_en_gcd, pc_en_p1, pc_en_p2, pc_hold_ex, pc_step_ex, pram_use_op,
       prime_res, regD_m1_eq0, regD_m1_nez, rRAM_str, rram_we_ex, rram_we_fib, set_done, sp_en, sp_en_ex,
       take_br, take_djnz, take_jump, use_cnt4, valid_d;
  wire [1:0] dec_d_sel;
  wire [2:0] ns_clear, ns_ex1, ns_ex2, ns_exec, ns_fib, ns_gcd, ns_idle, ns_out, ns_st1, ns_st2, ns_stop,
       state, state_d, state_no_rst;
  wire [3:0] cnt4, cnt4_d, cnt4_no_rst, cnt4_p1, cnt4_step, dec_a_sel;
  wire [4:0] fibN, fibN_d, fibN_m1;
  wire [7:0] a_d, a_next, a_next_ex, accA, accB, alu_add, alu_and, alu_div, alu_mod, alu_mul, alu_not,
       alu_or, ALU_out, alu_rol, alu_ror, alu_shl, alu_shr, alu_sub, alu_xor, b_d, b_next, c_d, c_next, d_d,
       d_next, fib_din, gcdA, gcdA_d, gcdA_next_loop, gcdA_sub, gcdB, gcdB_d, gcdB_next_loop, gcdB_sub,
       lcnt_d, lcnt_p1, load_cnt, PC, pc_d, pc_next_exec, pc_p1, pRAM_A, pram_a_run, regC, regD, regD_m1,
       rol_dbl, rRAM_A, rram_a_ex, rram_a_fib, rram_a_no_rst, rram_a_run, rRAM_Din, rram_din_run, SP, sp_d,
       sp_m1, sp_next_ex, sp_p1;
  wire [13:0] IR, pRAM_D;
  wire [15:0] fib0, fib0_d, fib1, fib1_d, fib_sum;
  wire [15:8] ror_dbl;
  wire [15:12] dec_out;

  RAMDualPort #(.AddrBits(8), .Bits(14)) pRAM (
    .A(pRAM_A), .Din(progIn), .str(progLoad), .C(clk), .ld(1'b1), .D(pRAM_D));
  RAMDualPort #(.AddrBits(8), .Bits(8)) rRAM (
    .A(rRAM_A), .Din(rRAM_Din), .str(rRAM_str), .C(clk), .ld(1'b1), .D(\output ));
  Seven_Seg_Hex seven_seg_hex_1 (.d(\output [7:4]), .dp(1'b0));
  Seven_Seg_Hex seven_seg_hex_2 (.d(\output [3:0]), .dp(1'b0));
  Register #(.Bits(3)) u_STATE (.D(state_d), .C(clk), .en(1'b1), .Q(state));
  Register #(.Bits(4)) u_cnt4 (.D(cnt4_d), .C(clk), .en(1'b1), .Q(cnt4));
  Register #(.Bits(8)) u_load_cnt (.D(lcnt_d), .C(clk), .en(1'b1), .Q(load_cnt));
  Register #(.Bits(14)) u_IR (.D(pRAM_D), .C(clk), .en(is_fetch), .Q(IR));
  Register #(.Bits(8)) u_PC (.D(pc_d), .C(clk), .en(pc_en), .Q(PC));
  Register #(.Bits(1)) valid_reg (.D(valid_d), .C(clk), .en(1'b1), .Q(valid));
  Register #(.Bits(1)) done_reg (.D(done_d), .C(clk), .en(1'b1), .Q(done));
  ROM #(.AddrBits(6), .Bits(16)) Decoder_ROM (
    .A(IR[13:8]), .sel(1'b1),
    .D({dec_out, dec_d_sel, dec_d_we, dec_c_sel, dec_c_we, dec_b_sel, dec_b_we, dec_a_we, dec_a_sel}));
  Add #(.Bits(4)) add_1 (.a(cnt4), .b(4'b0001), .c_i(1'b0), .s(cnt4_p1));  // open: c_o
  Comparator #(.Bits(4)) comparator_1 (.a(cnt4), .b(4'b1111), .eq(cnt4_is15));  // open: gt, lt
  Add #(.Bits(8)) add_2 (.a(load_cnt), .b(8'h1), .c_i(1'b0), .s(lcnt_p1));  // open: c_o
  Comparator #(.Bits(3)) comparator_2 (.a(state), .b(3'b000), .eq(is_clear));  // open: gt, lt
  Comparator #(.Bits(3)) comparator_3 (.a(state), .b(3'b001), .eq(is_idle));  // open: gt, lt
  Comparator #(.Bits(3)) comparator_4 (.a(state), .b(3'b010), .eq(is_fetch));  // open: gt, lt
  Comparator #(.Bits(3)) comparator_5 (.a(state), .b(3'b011), .eq(is_exec));  // open: gt, lt
  Comparator #(.Bits(3)) comparator_6 (.a(state), .b(3'b100), .eq(is_gcd));  // open: gt, lt
  Comparator #(.Bits(3)) comparator_7 (.a(state), .b(3'b101), .eq(is_fib));  // open: gt, lt
  Comparator #(.Bits(3)) comparator_8 (.a(state), .b(3'b110), .eq(is_stop));  // open: gt, lt
  Comparator #(.Bits(3)) comparator_9 (.a(state), .b(3'b111), .eq(is_out));  // open: gt, lt
  Multiplexer #(.Bits(8)) multiplexer_1 (.sel(progLoad), .in_0({8{1'b0}}), .in_1(lcnt_p1), .out(lcnt_d));
  Multiplexer #(.Bits(3)) multiplexer_2 (.sel(cnt4_is15), .in_0(3'b000), .in_1(3'b001), .out(ns_clear));
  Multiplexer #(.Bits(3)) multiplexer_3 (.sel(start), .in_0(3'b001), .in_1(3'b010), .out(ns_idle));
  or or_1 (clr_all, reset, is_clear);
  or or_2 (clr_pc_sp, clr_all, start);
  Comparator #(.Bits(6)) comparator_10 (.a(IR[13:8]), .b({6{1'b1}}), .eq(op_is_stop));  // open: gt, lt
  Comparator #(.Bits(6)) comparator_11 (.a(IR[13:8]), .b(6'b111100), .eq(op_is_gcd));  // open: gt, lt
  Comparator #(.Bits(6)) comparator_12 (.a(IR[13:8]), .b(6'b111101), .eq(op_is_fib));  // open: gt, lt
  Comparator #(.Bits(6)) comparator_13 (.a(IR[13:8]), .b(6'b111000), .eq(op_is_cmp));  // open: gt, lt
  Comparator #(.Bits(6)) comparator_14 (.a(IR[13:8]), .b(6'b111001), .eq(op_is_prime));  // open: gt, lt
  Comparator #(.Bits(6)) comparator_15 (.a(IR[13:8]), .b(6'b110100), .eq(op_is_djnz));  // open: gt, lt
  Comparator #(.Bits(6)) comparator_16 (.a(IR[13:8]), .b(6'b010010), .eq(op_is_pram));  // open: gt, lt
  Multiplexer #(.Bits(3)) multiplexer_4 (.sel(op_is_fib), .in_0(3'b010), .in_1(3'b101), .out(ns_ex1));
  Multiplexer #(.Bits(3)) multiplexer_5 (.sel(op_is_gcd), .in_0(ns_ex1), .in_1(3'b100), .out(ns_ex2));
  Multiplexer #(.Bits(3)) multiplexer_6 (.sel(op_is_stop), .in_0(ns_ex2), .in_1(3'b110), .out(ns_exec));
  Multiplexer #(.Bits(3)) multiplexer_7 (.sel(gcd_eq), .in_0(3'b100), .in_1(3'b010), .out(ns_gcd));
  Multiplexer #(.Bits(3)) multiplexer_8 (.sel(fib_done), .in_0(3'b101), .in_1(3'b010), .out(ns_fib));
  Multiplexer #(.Bits(3)) multiplexer_9 (.sel(progLoad), .in_0(3'b110), .in_1(3'b001), .out(ns_st1));
  Multiplexer #(.Bits(3)) multiplexer_10 (.sel(start), .in_0(ns_st1), .in_1(3'b010), .out(ns_st2));
  Multiplexer #(.Bits(3)) multiplexer_11 (.sel(result), .in_0(ns_st2), .in_1(3'b111), .out(ns_stop));
  Multiplexer #(.Bits(3)) multiplexer_12 (.sel(cnt4_is15), .in_0(3'b111), .in_1(3'b110), .out(ns_out));
  Comparator #(.Bits(2)) comparator_17 (.a(IR[13:12]), .b(2'b11), .eq(is_ctrl_grp));  // open: gt, lt
  Comparator #(.Bits(2)) comparator_18 (.a(IR[11:10]), .b(2'b00), .eq(is_sub_00));  // open: gt, lt
  Sub #(.Bits(8)) sub_1 (.a(regD), .b(8'h1), .c_i(1'b0), .s(regD_m1));  // open: c_o
  or or_3 (pc_hold_ex, op_is_stop, op_is_gcd, op_is_fib);
  Multiplexer #(.Selector_Bits(3), .Bits(3)) multiplexer_13 (
    .sel(state), .in_0(ns_clear), .in_1(ns_idle), .in_2(3'b011), .in_3(ns_exec), .in_4(ns_gcd),
    .in_5(ns_fib), .in_6(ns_stop), .in_7(ns_out), .out(state_no_rst));
  Multiplexer #(.Bits(4)) multiplexer_14 (.sel(cnt4_is15), .in_0(cnt4_p1), .in_1(4'b0000), .out(cnt4_step));
  or or_4 (use_cnt4, is_clear, is_out);
  and and_1 (set_done, is_out, cnt4_is15);
  or or_5 (clr_done_stop, result, start, progLoad);
  Multiplexer #(.Selector_Bits(2), .Bits(1)) multiplexer_15 (
    .sel(IR[9:8]), .in_0(1'b1), .in_1(eq), .in_2(gr), .in_3(ls), .out(br_cond));
  Comparator #(.Bits(8)) comparator_19 (.a(regD_m1), .b({8{1'b0}}), .eq(regD_m1_eq0));  // open: gt, lt
  Add #(.Bits(8)) add_3 (.a(PC), .b(8'h1), .c_i(1'b0), .s(pc_p1));  // open: c_o
  not not_1 (pc_step_ex, pc_hold_ex);
  Comparator #(.Bits(3)) comparator_20 (.a(state_d), .b(3'b110), .gt(ns_gt6), .eq(ns_eq6));  // open: lt
  and and_2 (pc_en_ex, is_exec, pc_step_ex);
  and and_3 (pc_en_gcd, is_gcd, gcd_eq);
  and and_4 (pc_en_fib, is_fib, fib_done);
  Multiplexer #(.Bits(3)) multiplexer_16 (.sel(reset), .in_0(state_no_rst), .in_1(3'b000), .out(state_d));
  Multiplexer #(.Bits(4)) multiplexer_17 (.sel(use_cnt4), .in_0(4'b0000), .in_1(cnt4_step), .out(cnt4_no_rst));
  not not_2 (keep_done_stop, clr_done_stop);
  and and_5 (take_br, is_ctrl_grp, is_sub_00, br_cond);
  not not_3 (regD_m1_nez, regD_m1_eq0);
  or or_6 (valid_d, ns_gt6, ns_eq6);
  and and_6 (hold_done, is_stop, done, keep_done_stop);
  Multiplexer #(.Bits(8)) multiplexer_18 (.sel(take_jump), .in_0(pc_p1), .in_1(IR[7:0]), .out(pc_next_exec));
  or or_7 (pc_en_p1, clr_pc_sp, pc_en_ex);
  or or_8 (pc_en_p2, pc_en_gcd, pc_en_fib);
  Multiplexer #(.Bits(4)) multiplexer_19 (.sel(reset), .in_0(cnt4_no_rst), .in_1(4'b0000), .out(cnt4_d));
  and and_7 (take_djnz, op_is_djnz, regD_m1_nez);
  or or_9 (done_no_rst, set_done, hold_done);
  or or_10 (take_jump, take_br, take_djnz);
  Multiplexer #(.Bits(8)) multiplexer_20 (.sel(clr_pc_sp), .in_0(pc_next_exec), .in_1({8{1'b0}}), .out(pc_d));
  or or_11 (pc_en, pc_en_p1, pc_en_p2);
  Multiplexer #(.Bits(1)) multiplexer_21 (.sel(reset), .in_0(done_no_rst), .in_1(1'b0), .out(done_d));
  Sub #(.Bits(8)) sub_2 (.a(SP), .b(8'h1), .c_i(1'b0), .s(sp_m1));  // open: c_o
  Add #(.Bits(8)) add_4 (.a(SP), .b(8'h1), .c_i(1'b0), .s(sp_p1));  // open: c_o
  and and_8 (sp_en_ex, is_exec, dec_out[15]);
  Multiplexer #(.Bits(8)) multiplexer_22 (.sel(dec_b_sel), .in_0(IR[7:0]), .in_1(accA), .out(b_next));
  and and_9 (b_en_ex, is_exec, dec_b_we);
  Multiplexer #(.Bits(8)) multiplexer_23 (.sel(dec_c_sel), .in_0(accA), .in_1(M), .out(c_next));
  and and_10 (c_en_ex, is_exec, dec_c_we);
  Multiplexer #(.Selector_Bits(2), .Bits(8)) multiplexer_24 (
    .sel(dec_d_sel), .in_0(accA), .in_1(N), .in_2(regD_m1), .in_3({8{1'b0}}), .out(d_next));
  and and_11 (d_en_ex, is_exec, dec_d_we);
  Multiplexer #(.Selector_Bits(3), .Bits(8)) multiplexer_25 (
    .sel(dec_a_sel[2:0]), .in_0(IR[7:0]), .in_1(accB), .in_2(regC), .in_3(regD), .in_4(SP), .in_5(\output ),
    .in_6(pRAM_D[7:0]), .in_7(ALU_out), .out(a_next_ex));
  and and_12 (a_en_ex, is_exec, dec_a_we);
  and and_13 (gcd_done_a, is_gcd, gcd_eq);
  and and_14 (pram_use_op, is_exec, op_is_pram);
  Multiplexer #(.Selector_Bits(2), .Bits(8)) multiplexer_26 (
    .sel(dec_out[14:13]), .in_0(IR[7:0]), .in_1(regC), .in_2(sp_m1), .in_3(SP), .out(rram_a_ex));
  Multiplexer #(.Bits(8)) multiplexer_27 (.sel(fib_step), .in_0(fib0[15:8]), .in_1(fib0[7:0]), .out(fib_din));
  and and_15 (rram_we_ex, is_exec, dec_out[12]);
  and and_16 (rram_we_fib, is_fib, fib_we_active);
  Multiplexer #(.Bits(8)) multiplexer_28 (.sel(IR[8]), .in_0(sp_m1), .in_1(sp_p1), .out(sp_next_ex));
  or or_12 (sp_en, clr_pc_sp, sp_en_ex);
  Multiplexer #(.Bits(8)) multiplexer_29 (.sel(clr_all), .in_0(b_next), .in_1({8{1'b0}}), .out(b_d));
  or or_13 (b_en, clr_all, b_en_ex);
  Multiplexer #(.Bits(8)) multiplexer_30 (.sel(clr_all), .in_0(c_next), .in_1({8{1'b0}}), .out(c_d));
  or or_14 (c_en, clr_all, c_en_ex);
  Multiplexer #(.Bits(8)) multiplexer_31 (.sel(clr_all), .in_0(d_next), .in_1({8{1'b0}}), .out(d_d));
  or or_15 (d_en, clr_all, d_en_ex);
  Multiplexer #(.Bits(8)) multiplexer_32 (.sel(is_gcd), .in_0(a_next_ex), .in_1(gcdA), .out(a_next));
  or or_16 (a_en, clr_all, a_en_ex, gcd_done_a);
  Multiplexer #(.Bits(8)) multiplexer_33 (.sel(pram_use_op), .in_0(PC), .in_1(IR[7:0]), .out(pram_a_run));
  Multiplexer #(.Bits(8)) multiplexer_34 (.sel(fib_step), .in_0(8'ha), .in_1(8'hb), .out(rram_a_fib));
  Multiplexer #(.Bits(8)) multiplexer_35 (.sel(is_fib), .in_0(accA), .in_1(fib_din), .out(rram_din_run));
  or or_17 (rRAM_str, rram_we_ex, rram_we_fib, is_clear);
  Multiplexer #(.Bits(8)) multiplexer_36 (.sel(clr_pc_sp), .in_0(sp_next_ex), .in_1({8{1'b0}}), .out(sp_d));
  Multiplexer #(.Bits(8)) multiplexer_37 (.sel(clr_all), .in_0(a_next), .in_1({8{1'b0}}), .out(a_d));
  Multiplexer #(.Bits(8)) multiplexer_38 (.sel(progLoad), .in_0(pram_a_run), .in_1(load_cnt), .out(pRAM_A));
  Multiplexer #(.Bits(8)) multiplexer_39 (.sel(is_fib), .in_0(rram_a_ex), .in_1(rram_a_fib), .out(rram_a_run));
  Multiplexer #(.Bits(8)) multiplexer_40 (.sel(is_clear), .in_0(rram_din_run), .in_1({8{1'b0}}), .out(rRAM_Din));
  Register #(.Bits(8)) u_accB (.D(b_d), .C(clk), .en(b_en), .Q(accB));
  Register #(.Bits(8)) u_regC (.D(c_d), .C(clk), .en(c_en), .Q(regC));
  Register #(.Bits(8)) u_regD (.D(d_d), .C(clk), .en(d_en), .Q(regD));
  Register #(.Bits(8)) u_SP (.D(sp_d), .C(clk), .en(sp_en), .Q(SP));
  Register #(.Bits(8)) u_accA (.D(a_d), .C(clk), .en(a_en), .Q(accA));
  Multiplexer #(.Bits(8)) multiplexer_41 (
    .sel(use_cnt4), .in_0(rram_a_run), .in_1({4'b0000, cnt4}), .out(rram_a_no_rst));
  Multiplexer #(.Bits(8)) multiplexer_42 (.sel(reset), .in_0(rram_a_no_rst), .in_1({8{1'b0}}), .out(rRAM_A));
  Add #(.Bits(8)) add_5 (.a(accA), .b(accB), .c_i(1'b0), .s(alu_add));  // open: c_o
  Sub #(.Bits(8)) sub_3 (.a(accA), .b(accB), .c_i(1'b0), .s(alu_sub));  // open: c_o
  Mul #(.Bits(4)) mul_1 (.a(accA[3:0]), .b(accB[3:0]), .mul(alu_mul));
  Div #(.Bits(8)) div_1 (.a(accA), .b(accB), .q(alu_div), .r(alu_mod));
  assign alu_and = accA & accB;  // And and_17, 8 bits wide
  assign alu_or = accA | accB;  // Or or_18, 8 bits wide
  assign alu_xor = accA ^ accB;  // XOr xor_1, 8 bits wide
  assign alu_not = ~accA;  // Not not_4, 8 bits wide
  BarrelShifter #(.Bits(8), .direction("left")) barrelshifter_1 (.in(accA), .shift({1'b0, accB[2:0]}), .out(alu_shl));
  BarrelShifter #(.Bits(8), .direction("right")) barrelshifter_2 (.in(accA), .shift({1'b0, accB[2:0]}), .out(alu_shr));
  BarrelShifter #(.Bits(16), .direction("left")) barrelshifter_3 (
    .in({accA, accA}), .shift({2'b00, accB[2:0]}), .out({alu_rol, rol_dbl}));
  BarrelShifter #(.Bits(16), .direction("right")) barrelshifter_4 (
    .in({accA, accA}), .shift({2'b00, accB[2:0]}), .out({ror_dbl, alu_ror}));
  Comparator #(.Signed("true"), .Bits(8)) comparator_21 (.a(accA), .b(accB), .gt(cmp_gr), .eq(cmp_eq), .lt(cmp_ls));
  ROM #(.AddrBits(8), .Bits(1)) Prime_ROM (.A(accA), .sel(1'b1), .D(prime_res));
  Multiplexer #(.Bits(1)) multiplexer_43 (.sel(op_is_prime), .in_0(cmp_eq), .in_1(prime_res), .out(eq_target));
  or or_19 (flags_update_op, op_is_cmp, op_is_prime);
  Multiplexer #(.Selector_Bits(4), .Bits(8)) multiplexer_44 (
    .sel(IR[11:8]), .in_0(alu_add), .in_1(alu_sub), .in_2(alu_mul), .in_3({8{1'b0}}), .in_4(alu_div),
    .in_5(alu_mod), .in_6({8{1'b0}}), .in_7({8{1'b0}}), .in_8(alu_and), .in_9(alu_or), .in_10(alu_xor),
    .in_11(alu_not), .in_12(alu_shl), .in_13(alu_shr), .in_14(alu_rol), .in_15(alu_ror), .out(ALU_out));
  Multiplexer #(.Bits(1)) multiplexer_45 (.sel(clr_all), .in_0(eq_target), .in_1(1'b0), .out(eq_d));
  and and_18 (eq_we_ex, is_exec, flags_update_op);
  Multiplexer #(.Bits(1)) multiplexer_46 (.sel(clr_all), .in_0(cmp_gr), .in_1(1'b0), .out(gr_d));
  and and_19 (gr_we_ex, is_exec, op_is_cmp);
  Multiplexer #(.Bits(1)) multiplexer_47 (.sel(clr_all), .in_0(cmp_ls), .in_1(1'b0), .out(ls_d));
  or or_20 (eq_en, clr_all, eq_we_ex);
  or or_21 (gr_en, clr_all, gr_we_ex);
  Register #(.Bits(1)) FLAG_EQ (.D(eq_d), .C(clk), .en(eq_en), .Q(eq));
  Register #(.Bits(1)) FLAG_GR (.D(gr_d), .C(clk), .en(gr_en), .Q(gr));
  Register #(.Bits(1)) FLAG_LS (.D(ls_d), .C(clk), .en(gr_en), .Q(ls));
  Comparator #(.Bits(8)) comparator_22 (.a(gcdA), .b(gcdB), .gt(gcd_gt), .eq(gcd_eq), .lt(gcd_lt));
  Sub #(.Bits(8)) sub_4 (.a(gcdA), .b(gcdB), .c_i(1'b0), .s(gcdA_sub));  // open: c_o
  Sub #(.Bits(8)) sub_5 (.a(gcdB), .b(gcdA), .c_i(1'b0), .s(gcdB_sub));  // open: c_o
  Comparator #(.Bits(5)) comparator_23 (.a(fibN), .b({5{1'b0}}), .eq(fib_n_is0));  // open: gt, lt
  Sub #(.Bits(5)) sub_6 (.a(fibN), .b(5'b00001), .c_i(1'b0), .s(fibN_m1));  // open: c_o
  Add #(.Bits(16)) add_6 (.a(fib0), .b(fib1), .c_i(1'b0), .s(fib_sum));  // open: c_o
  and and_20 (fib_init, is_exec, op_is_fib);
  Multiplexer #(.Bits(8)) multiplexer_48 (.sel(gcd_gt), .in_0(gcdA), .in_1(gcdA_sub), .out(gcdA_next_loop));
  and and_21 (gcd_init, is_exec, op_is_gcd);
  Multiplexer #(.Bits(8)) multiplexer_49 (.sel(gcd_lt), .in_0(gcdB), .in_1(gcdB_sub), .out(gcdB_next_loop));
  not not_5 (fib_not_done, fib_n_is0);
  Multiplexer #(.Bits(5)) multiplexer_50 (.sel(is_fib), .in_0(accA[4:0]), .in_1(fibN_m1), .out(fibN_d));
  Multiplexer #(.Bits(16)) multiplexer_51 (.sel(is_fib), .in_0({16{1'b0}}), .in_1(fib1), .out(fib0_d));
  Multiplexer #(.Bits(16)) multiplexer_52 (.sel(is_fib), .in_0(16'h1), .in_1(fib_sum), .out(fib1_d));
  Multiplexer #(.Bits(8)) multiplexer_53 (.sel(is_gcd), .in_0(accA), .in_1(gcdA_next_loop), .out(gcdA_d));
  or or_22 (gcd_en, gcd_init, is_gcd);
  Multiplexer #(.Bits(8)) multiplexer_54 (.sel(is_gcd), .in_0(accB), .in_1(gcdB_next_loop), .out(gcdB_d));
  and and_22 (fib_step_en, is_fib, fib_not_done);
  Register #(.Bits(8)) u_gcdA (.D(gcdA_d), .C(clk), .en(gcd_en), .Q(gcdA));
  Register #(.Bits(8)) u_gcdB (.D(gcdB_d), .C(clk), .en(gcd_en), .Q(gcdB));
  or or_23 (fib_regs_en, fib_init, fib_step_en);
  and and_23 (fib_we_active, is_fib, fib_n_is0);
  Register #(.Bits(5)) u_fibN (.D(fibN_d), .C(clk), .en(fib_regs_en), .Q(fibN));
  Register #(.Bits(16)) u_fib0 (.D(fib0_d), .C(clk), .en(fib_regs_en), .Q(fib0));
  Register #(.Bits(16)) u_fib1 (.D(fib1_d), .C(clk), .en(fib_regs_en), .Q(fib1));
  Register #(.Bits(1)) fib_step_reg (.D(fib_we_active), .C(clk), .en(is_fib), .Q(fib_step));
  and and_24 (fib_done, fib_we_active, fib_step);

  // Other names for the same wires on the sheet: accA_double[15:0] = {accA, accA}; fib_n_init[4:0] = accA[4:0];
  //   mul_a4[3:0] = accA[3:0]; b_rot3[2:0] = accB[2:0]; mul_b4[3:0] = accB[3:0]; shift_amt4[2:0] = accB[2:0];
  //   shift_amt5[2:0] = accB[2:0]; cnt4_8[3:0] = cnt4; dec_a_sel3[2:0] = dec_a_sel[2:0];
  //   dec_out[11:0] = {dec_d_sel, dec_d_we, dec_c_sel, dec_c_we, dec_b_sel, dec_b_we, dec_a_we, dec_a_sel};
  //   dec_ram_we = dec_out[12]; dec_ram_addr[1:0] = dec_out[14:13]; dec_sp_we = dec_out[15]; fib0_lo[7:0] = fib0[7:0];
  //   fib0_hi[7:0] = fib0[15:8]; Operand[7:0] = IR[7:0]; op0 = IR[8]; op10[1:0] = IR[9:8]; op30[3:0] = IR[11:8];
  //   Opcode[5:0] = IR[13:8]; IR_11_10[1:0] = IR[11:10]; op54[1:0] = IR[13:12]; pRAM_low[7:0] = pRAM_D[7:0];
  //   rol_dbl[15:8] = alu_rol; ror_dbl[7:0] = alu_ror; rRAM_D[7:0] = \output 

  // Notes on the sheet:
  //   contents of Decoder_ROM (hex, n*v repeats v):
  //   0,10,20,0,11,60,80,200,12,13,14,0,180,600,0,0,15,1000,16,0,2015
  //   ,3000,0,0,d000,e015,6*0,16*17,4*0,a00
  //   contents of Prime_ROM (hex, n*v repeats v):
  //   0,0,1,1,0,1,0,1,0,0,0,1,0,1,0,0,0,1,0,1,0,0,0,1,5*0,1,0,1,5*0
  //   ,1,0,0,0,1,0,1,0,0,0,1,5*0,1,5*0,1,0,1,5*0,1,0,0,0,1,0,1,5*0,1
  //   ,0,0,0,1,5*0,1,7*0,1,0,0,0,1,0,1,0,0,0,1,0,1,0,0,0,1,13*0,1,0,0,0
  //   ,1,5*0,1,0,1,9*0,1,0,1,5*0,1,5*0,1,0,0,0,1,5*0,1,5*0,1,0,1,9*0
  //   ,1,0,1,0,0,0,1,0,1,11*0,1,11*0,1,0,0,0,1,0,1,0,0,0,1,5*0,1,0,1
  //   ,9*0,1
endmodule
